// Logisim project AFlix.circ as structural Verilog: 19 circuits, main circuit sketch
module FULLADDER (
  input  Ci,
  input  A,
  input  B,
  output S,
  output Co
);

  wire and_1_out, and_2_out, xor_1_out;

  xor xor_1 (xor_1_out, A, B);
  and and_1 (and_1_out, A, B);
  xor xor_2 (S, xor_1_out, Ci);
  and and_2 (and_2_out, xor_1_out, Ci);
  or or_1 (Co, and_2_out, and_1_out);
endmodule

module ALU1 (
  input  A,
  input  B,
  input  AINV,
  input  BINV,
  input  Ci,
  input  OP_XOR,
  input  OP_SUM,
  input  OP_OR,
  input  OP_AND,
  output Co,
  output R
);

  wire and_1_out, fulladder_1_s, or_1_out, xor_1_out, xor_2_out, xor_3_out;

  xor xor_1 (xor_1_out, A, AINV);
  FULLADDER fulladder_1 (.Ci(Ci), .A(xor_1_out), .B(xor_2_out), .S(fulladder_1_s), .Co(Co));
  assign R = OP_SUM ? fulladder_1_s : 1'bz;  // Controlled_Buffer controlled_buffer_1
  or or_1 (or_1_out, xor_1_out, xor_2_out);
  assign R = OP_OR ? or_1_out : 1'bz;  // Controlled_Buffer controlled_buffer_2
  Pull_Resistor pull_resistor_1 (.node(R));
  and and_1 (and_1_out, xor_1_out, xor_2_out);
  assign R = OP_AND ? and_1_out : 1'bz;  // Controlled_Buffer controlled_buffer_3
  xor xor_2 (xor_2_out, B, BINV);
  assign R = OP_XOR ? xor_3_out : 1'bz;  // Controlled_Buffer controlled_buffer_4
  xor xor_3 (xor_3_out, xor_2_out, xor_1_out);
endmodule

module ALU16 (
  input  OP_AINV,
  input  OP_BINV,
  input  OP_SUM,
  input  OP_OR,
  input  OP_AND,
  input  Ci,
  input  OP_XOR,
  input  LSL,
  input  LSR,
  input  [15:0] A,
  input  [15:0] B,
  output [15:0] R,
  output [3:0] F
);

  wire alu1_1_co, alu1_2_co, alu1_3_co, alu1_4_co, alu1_5_co, alu1_6_co, alu1_7_co, alu1_8_co, alu1_9_co,
       alu1_10_co, alu1_11_co, alu1_12_co, alu1_13_co, alu1_14_co, alu1_15_co, alu1_16_co,
       controlled_buffer_5_out, del_not16_1_q, del_not16_3_q, del_not16_4_q, nor_1_out, nor_2_out, or_1_out,
       xor_1_out;
  wire [3:0] pull_resistor_1_node;
  wire [15:0] AT, BT, controlled_buffer_11_out, controlled_buffer_12_out, pull_resistor_5_node,
       shifter_1_out, shifter_2_out;

  Pull_Resistor pull_resistor_1 (.node(pull_resistor_1_node[0]));
  Pull_Resistor pull_resistor_2 (.node(pull_resistor_1_node[1]));
  Pull_Resistor pull_resistor_3 (.node(pull_resistor_1_node[2]));
  Pull_Resistor pull_resistor_4 (.node(pull_resistor_1_node[3]));
  assign pull_resistor_1_node[0] = OP_SUM ? alu1_1_co : 1'bz;  // Controlled_Buffer controlled_buffer_1
  assign pull_resistor_1_node[1] = OP_SUM ? xor_1_out : 1'bz;  // Controlled_Buffer controlled_buffer_2
  assign pull_resistor_1_node[2] = OP_SUM ? pull_resistor_5_node[15] : 1'bz;  // Controlled_Buffer controlled_buffer_3
  assign pull_resistor_1_node[3] = OP_SUM ? controlled_buffer_5_out : 1'bz;  // Controlled_Buffer controlled_buffer_4
  DEL_NOT16 del_not16_1 (.D(del_not16_1_q), .Q(del_not16_1_q));
  DEL_NOT16 del_not16_2 (.D(del_not16_3_q), .Q(del_not16_1_q));
  DEL_NOT16 del_not16_3 (.D(del_not16_4_q), .Q(del_not16_3_q));
  DEL_NOT16 del_not16_4 (.Q(del_not16_4_q));  // open: D
  xor xor_1 (xor_1_out, alu1_1_co, alu1_2_co);
  assign controlled_buffer_5_out = OP_SUM ? nor_1_out : 1'bz;  // Controlled_Buffer controlled_buffer_5
  nor nor_1 (nor_1_out, pull_resistor_5_node[0], pull_resistor_5_node[1], pull_resistor_5_node[2], pull_resistor_5_node[3], pull_resistor_5_node[4], pull_resistor_5_node[5], pull_resistor_5_node[6], pull_resistor_5_node[7], pull_resistor_5_node[8], pull_resistor_5_node[9], pull_resistor_5_node[10], pull_resistor_5_node[11], pull_resistor_5_node[12], pull_resistor_5_node[13], pull_resistor_5_node[14], pull_resistor_5_node[15]);
  assign AT = or_1_out ? A : 16'bz;  // Controlled_Buffer controlled_buffer_6
  assign BT = or_1_out ? B : 16'bz;  // Controlled_Buffer controlled_buffer_7
  Register #(.width(4)) register_1 (.D(pull_resistor_1_node), .en(OP_SUM), .clk(del_not16_1_q), .Q(F));  // open: clr
  or or_1 (or_1_out, OP_BINV, OP_AINV, OP_OR, OP_AND, OP_SUM, LSR, LSL);
  ALU1 alu1_1 (
    .A(AT[15]), .B(BT[15]), .AINV(OP_AINV), .BINV(OP_BINV), .Ci(alu1_2_co), .OP_XOR(OP_XOR), .OP_SUM(OP_SUM),
    .OP_OR(OP_OR), .OP_AND(OP_AND), .Co(alu1_1_co), .R(pull_resistor_5_node[15]));
  ALU1 alu1_2 (
    .A(AT[14]), .B(BT[14]), .AINV(OP_AINV), .BINV(OP_BINV), .Ci(alu1_3_co), .OP_XOR(OP_XOR), .OP_SUM(OP_SUM),
    .OP_OR(OP_OR), .OP_AND(OP_AND), .Co(alu1_2_co), .R(pull_resistor_5_node[14]));
  ALU1 alu1_3 (
    .A(AT[13]), .B(BT[13]), .AINV(OP_AINV), .BINV(OP_BINV), .Ci(alu1_4_co), .OP_XOR(OP_XOR), .OP_SUM(OP_SUM),
    .OP_OR(OP_OR), .OP_AND(OP_AND), .Co(alu1_3_co), .R(pull_resistor_5_node[13]));
  ALU1 alu1_4 (
    .A(AT[12]), .B(BT[12]), .AINV(OP_AINV), .BINV(OP_BINV), .Ci(alu1_5_co), .OP_XOR(OP_XOR), .OP_SUM(OP_SUM),
    .OP_OR(OP_OR), .OP_AND(OP_AND), .Co(alu1_4_co), .R(pull_resistor_5_node[12]));
  ALU1 alu1_5 (
    .A(AT[11]), .B(BT[11]), .AINV(OP_AINV), .BINV(OP_BINV), .Ci(alu1_6_co), .OP_XOR(OP_XOR), .OP_SUM(OP_SUM),
    .OP_OR(OP_OR), .OP_AND(OP_AND), .Co(alu1_5_co), .R(pull_resistor_5_node[11]));
  ALU1 alu1_6 (
    .A(AT[10]), .B(BT[10]), .AINV(OP_AINV), .BINV(OP_BINV), .Ci(alu1_7_co), .OP_XOR(OP_XOR), .OP_SUM(OP_SUM),
    .OP_OR(OP_OR), .OP_AND(OP_AND), .Co(alu1_6_co), .R(pull_resistor_5_node[10]));
  ALU1 alu1_7 (
    .A(AT[9]), .B(BT[9]), .AINV(OP_AINV), .BINV(OP_BINV), .Ci(alu1_8_co), .OP_XOR(OP_XOR), .OP_SUM(OP_SUM),
    .OP_OR(OP_OR), .OP_AND(OP_AND), .Co(alu1_7_co), .R(pull_resistor_5_node[9]));
  assign R = LSL ? shifter_1_out : 16'bz;  // Controlled_Buffer controlled_buffer_8
  assign R = LSR ? shifter_2_out : 16'bz;  // Controlled_Buffer controlled_buffer_9
  assign R = nor_2_out ? pull_resistor_5_node : 16'bz;  // Controlled_Buffer controlled_buffer_10
  ALU1 alu1_8 (
    .A(AT[8]), .B(BT[8]), .AINV(OP_AINV), .BINV(OP_BINV), .Ci(alu1_9_co), .OP_XOR(OP_XOR), .OP_SUM(OP_SUM),
    .OP_OR(OP_OR), .OP_AND(OP_AND), .Co(alu1_8_co), .R(pull_resistor_5_node[8]));
  assign controlled_buffer_11_out = LSL ? pull_resistor_5_node : 16'bz;  // Controlled_Buffer controlled_buffer_11
  assign controlled_buffer_12_out = LSR ? pull_resistor_5_node : 16'bz;  // Controlled_Buffer controlled_buffer_12
  nor nor_2 (nor_2_out, LSR, LSL);
  Shifter #(.width(16)) shifter_1 (.in(controlled_buffer_11_out), .\dist (BT[3:0]), .out(shifter_1_out));
  Pull_Resistor pull_resistor_5 (.node(pull_resistor_5_node));
  Shifter #(.shift("lr"), .width(16)) shifter_2 (.in(controlled_buffer_12_out), .\dist (BT[3:0]), .out(shifter_2_out));
  Pull_Resistor pull_resistor_6 (.node(BT[3:0]));
  ALU1 alu1_9 (
    .A(AT[7]), .B(BT[7]), .AINV(OP_AINV), .BINV(OP_BINV), .Ci(alu1_10_co), .OP_XOR(OP_XOR), .OP_SUM(OP_SUM),
    .OP_OR(OP_OR), .OP_AND(OP_AND), .Co(alu1_9_co), .R(pull_resistor_5_node[7]));
  ALU1 alu1_10 (
    .A(AT[6]), .B(BT[6]), .AINV(OP_AINV), .BINV(OP_BINV), .Ci(alu1_11_co), .OP_XOR(OP_XOR), .OP_SUM(OP_SUM),
    .OP_OR(OP_OR), .OP_AND(OP_AND), .Co(alu1_10_co), .R(pull_resistor_5_node[6]));
  ALU1 alu1_11 (
    .A(AT[5]), .B(BT[5]), .AINV(OP_AINV), .BINV(OP_BINV), .Ci(alu1_12_co), .OP_XOR(OP_XOR), .OP_SUM(OP_SUM),
    .OP_OR(OP_OR), .OP_AND(OP_AND), .Co(alu1_11_co), .R(pull_resistor_5_node[5]));
  ALU1 alu1_12 (
    .A(AT[4]), .B(BT[4]), .AINV(OP_AINV), .BINV(OP_BINV), .Ci(alu1_13_co), .OP_XOR(OP_XOR), .OP_SUM(OP_SUM),
    .OP_OR(OP_OR), .OP_AND(OP_AND), .Co(alu1_12_co), .R(pull_resistor_5_node[4]));
  ALU1 alu1_13 (
    .A(AT[3]), .B(BT[3]), .AINV(OP_AINV), .BINV(OP_BINV), .Ci(alu1_14_co), .OP_XOR(OP_XOR), .OP_SUM(OP_SUM),
    .OP_OR(OP_OR), .OP_AND(OP_AND), .Co(alu1_13_co), .R(pull_resistor_5_node[3]));
  ALU1 alu1_14 (
    .A(AT[2]), .B(BT[2]), .AINV(OP_AINV), .BINV(OP_BINV), .Ci(alu1_15_co), .OP_XOR(OP_XOR), .OP_SUM(OP_SUM),
    .OP_OR(OP_OR), .OP_AND(OP_AND), .Co(alu1_14_co), .R(pull_resistor_5_node[2]));
  ALU1 alu1_15 (
    .A(AT[1]), .B(BT[1]), .AINV(OP_AINV), .BINV(OP_BINV), .Ci(alu1_16_co), .OP_XOR(OP_XOR), .OP_SUM(OP_SUM),
    .OP_OR(OP_OR), .OP_AND(OP_AND), .Co(alu1_15_co), .R(pull_resistor_5_node[1]));
  ALU1 alu1_16 (
    .A(AT[0]), .B(BT[0]), .AINV(OP_AINV), .BINV(OP_BINV), .Ci(Ci), .OP_XOR(OP_XOR), .OP_SUM(OP_SUM),
    .OP_OR(OP_OR), .OP_AND(OP_AND), .Co(alu1_16_co), .R(pull_resistor_5_node[0]));

  // Other names for the same wires on the sheet: AIT = OP_AINV; ANT = OP_AND; BIT = OP_BINV; CiT = Ci; LST = LSL;
  //   ORT = OP_OR; RST = LSR; RT[15:0] = R; S_AMT[3:0] = BT[3:0]; SUT = OP_SUM; XOT = OP_XOR
endmodule

module DEL_NOT16 (
  input  D,
  output Q
);

  wire not_1_out, not_2_out, not_3_out, not_4_out, not_5_out, not_6_out, not_8_out, not_9_out, not_10_out,
       not_11_out, not_12_out, not_13_out, not_14_out, not_15_out, not_16_out, not_17_out, not_18_out,
       not_19_out, not_20_out, not_21_out, not_22_out, not_23_out, not_24_out;

  not not_1 (not_1_out, not_4_out);
  not not_2 (not_2_out, not_5_out);
  not not_3 (not_3_out, not_6_out);
  not not_4 (not_4_out, not_2_out);
  not not_5 (not_5_out, not_3_out);
  not not_6 (not_6_out, not_13_out);
  not not_7 (Q, not_10_out);
  not not_8 (not_8_out, not_11_out);
  not not_9 (not_9_out, not_12_out);
  not not_10 (not_10_out, not_8_out);
  not not_11 (not_11_out, not_9_out);
  not not_12 (not_12_out, not_19_out);
  not not_13 (not_13_out, not_16_out);
  not not_14 (not_14_out, not_17_out);
  not not_15 (not_15_out, not_18_out);
  not not_16 (not_16_out, not_14_out);
  not not_17 (not_17_out, not_15_out);
  not not_18 (not_18_out, D);
  not not_19 (not_19_out, not_22_out);
  not not_20 (not_20_out, not_23_out);
  not not_21 (not_21_out, not_24_out);
  not not_22 (not_22_out, not_20_out);
  not not_23 (not_23_out, not_21_out);
  not not_24 (not_24_out, not_1_out);
endmodule

module HWSTACK (
  input  [15:0] HWSTK_I,
  input  POP,
  input  PUSH,
  input  [15:0] RAM_O,
  output [15:0] HWSTK_O,
  output [15:0] RAM_ADDR_I,
  output [15:0] RAM_DATA_I
);

  wire del_not16_1_q, del_not16_2_q, del_not16_3_q, del_not16_4_q, del_not16_5_q, del_not16_6_q,
       del_not16_7_q, or_1_out, or_2_out;
  wire [7:0] SC_q, SP_q, subtractor_1_out;
  wire [15:0] controlled_buffer_1_out;

  DEL_NOT16 del_not16_1 (.D(del_not16_2_q), .Q(del_not16_1_q));
  DEL_NOT16 del_not16_2 (.D(POP), .Q(del_not16_2_q));
  Counter SC (
    .load(POP), .up(PUSH), .count(or_1_out), .clk(or_1_out), .D(subtractor_1_out), .Q(SC_q));  // open: clr, carry
  or or_1 (or_1_out, del_not16_1_q, PUSH);
  LED LED_PUSH (.in(PUSH));
  LED LED_POP (.in(POP));
  DEL_NOT16 del_not16_3 (.D(POP), .Q(del_not16_3_q));
  DEL_NOT16 del_not16_4 (.D(del_not16_3_q), .Q(del_not16_4_q));
  Subtractor subtractor_1 (.a(SP_q), .b(8'h1), .out(subtractor_1_out));  // open: bin, bout
  DEL_NOT16 del_not16_5 (.D(del_not16_4_q), .Q(del_not16_5_q));
  or or_2 (or_2_out, del_not16_4_q, PUSH);
  Register #(.width(16)) STKOUT (.D(controlled_buffer_1_out), .clk(del_not16_6_q), .Q(HWSTK_O));  // open: en, clr
  DEL_NOT16 del_not16_6 (.D(del_not16_5_q), .Q(del_not16_6_q));
  Register SP (.D(SC_q), .en(del_not16_7_q), .clk(del_not16_7_q), .Q(SP_q));  // open: clr
  DEL_NOT16 del_not16_7 (.D(or_2_out), .Q(del_not16_7_q));
  assign controlled_buffer_1_out = POP ? RAM_O : 16'bz;  // Controlled_Buffer controlled_buffer_1
  assign RAM_ADDR_I = {{8{1'b0}}, SP_q};  // Bit_Extender bit_extender_1
  assign RAM_DATA_I = PUSH ? HWSTK_I : 16'bz;  // Controlled_Buffer controlled_buffer_2
endmodule

module sketch (
  input  in_1
);

  wire CLK, decoder_1_out0, decoder_1_out1, decoder_1_out2, decoder_1_out3, decoder_1_out4, decoder_2_out0,
       decoder_2_out1, decoder_2_out2, decoder_2_out3, decoder_2_out4, del_not16_1_q, del_not16_2_q, DESP,
       DIN_ENB, JMP, JSR, LDSP, not_1_out, not_2_out, not_3_out, or_1_out, PHI, PHR, PLR, RAM_ADDRIN_ENBL,
       RDSP, REG_ENABLE, RegCol_Enb, RFI, RFS, RIP, RSA, RSB, RSC, RSD, RSH, RSL, RSX, SRST, stack256_1_p9,
       STACK_INSTR, WSA, WSB, WSC, WSD, WSH, WSL, WSX, xor_1_out, xor_2_out, xor_3_out, xor_4_out, xor_6_out,
       xor_7_out, xor_8_out, xor_9_out, xor_10_out, xor_11_out, xor_12_out, xor_13_out, xor_14_out,
       xor_15_out, xor_16_out, xor_17_out, xor_18_out, xor_19_out, xor_20_out, xor_21_out, xor_23_out,
       xor_24_out, xor_25_out, xor_26_out, xor_27_out, xor_28_out, xor_29_out, xor_30_out, xor_31_out,
       XOR_RAM_STACK_REQ_out;
  wire [2:0] bit_extender_1_out, bit_extender_4_out, controlled_buffer_13_out, controlled_buffer_25_out;
  wire [7:0] controlled_buffer_36_out, HI8, LO8;
  wire [15:0] controlled_buffer_8_out, controlled_buffer_35_out, controlled_buffer_37_out, groupinglogic_1_x,
       HI16, IP, JMP_DEST, LO16, ram_1_dout, RAM_Addr, RAM_VAL, regcol_1_dout, RegCol_DIN, RegCol_Out,
       stack256_1_p8, stack256_1_p10, X16;
  wire [23:0] rom_1_data;
  wire [31:0] groupinglogic_1_alu, groupinglogic_1_iload, groupinglogic_1_misc, groupinglogic_1_reserved1,
       groupinglogic_1_reserved2, groupinglogic_1_rload, groupinglogic_1_stack, groupinglogic_1_store;

  // Digital_Oscilloscope #(.frontlines("both"), .nState(8)) Oszi: pin names not known; wires that end beside it: CLK
  assign JMP = in_1 ? in_1 : 1'bz;  // Controlled_Buffer controlled_buffer_1
  LowClock u_CLK (.CLKSIG(CLK));
  IP ip_1 (.JMP(JMP), .CLK(CLK), .JMPLOC(JMP_DEST), .IPOUT(IP));
  ROM #(.addrWidth(16), .dataWidth(24)) rom_1 (.addr(IP), .data(rom_1_data));
  assign WSX = PLR ? PLR : 1'bz;  // Controlled_Buffer controlled_buffer_2
  assign WSA = PLR ? decoder_1_out0 : 1'bz;  // Controlled_Buffer controlled_buffer_3
  assign WSB = PLR ? decoder_1_out1 : 1'bz;  // Controlled_Buffer controlled_buffer_4
  Pull_Resistor pull_resistor_1 (.node(JMP));
  GroupingLogic groupinglogic_1 (
    .Instruction(rom_1_data), .ILOAD(groupinglogic_1_iload), .RLOAD(groupinglogic_1_rload),
    .STORE(groupinglogic_1_store), .ALU(groupinglogic_1_alu), .HI(LO8), .LO(HI8), .X(groupinglogic_1_x),
    .STACK(groupinglogic_1_stack), .MISC(groupinglogic_1_misc), .RESERVED1(groupinglogic_1_reserved1),
    .RESERVED2(groupinglogic_1_reserved2));
  Bit_Extender #(.out_width(3), .\type ("zero")) bit_extender_1 (.in(HI8), .out(bit_extender_1_out));
  Decoder #(.enable("false"), .select(3)) decoder_1 (
    .out0(decoder_1_out0), .out1(decoder_1_out1), .out2(decoder_1_out2), .out3(decoder_1_out3),
    .out4(decoder_1_out4), .sel(bit_extender_1_out));  // open: out5, out6, out7
  assign WSC = PLR ? decoder_1_out2 : 1'bz;  // Controlled_Buffer controlled_buffer_5
  assign WSD = PLR ? decoder_1_out3 : 1'bz;  // Controlled_Buffer controlled_buffer_6
  assign JMP = PLR ? decoder_1_out4 : 1'bz;  // Controlled_Buffer controlled_buffer_7
  Adder #(.width(16)) adder_1 (.a(controlled_buffer_8_out), .b(16'h1), .out(JMP_DEST));  // open: cin, cout
  assign controlled_buffer_8_out = JMP ? RegCol_DIN : 16'bz;  // Controlled_Buffer controlled_buffer_8
  assign HI16 = {{8{1'b0}}, HI8};  // Bit_Extender bit_extender_2
  assign LO16 = {{8{1'b0}}, LO8};  // Bit_Extender bit_extender_3
  assign RAM_Addr = RAM_ADDRIN_ENBL ? groupinglogic_1_x : 16'bz;  // Controlled_Buffer controlled_buffer_9
  assign X16 = not_1_out ? groupinglogic_1_x : 16'bz;  // Controlled_Buffer controlled_buffer_10
  assign X16 = RIP ? IP : 16'bz;  // Controlled_Buffer controlled_buffer_11
  not not_1 (not_1_out, RIP);
  assign RSX = PHR ? PHR : 1'bz;  // Controlled_Buffer controlled_buffer_12
  assign controlled_buffer_13_out = RSA ? 3'b000 : 3'bz;  // Controlled_Buffer controlled_buffer_13
  assign controlled_buffer_13_out = RSB ? 3'b001 : 3'bz;  // Controlled_Buffer controlled_buffer_14
  // Probe on RegCol_DIN
  Pull_Resistor pull_resistor_2 (.node(WSD));
  Pull_Resistor pull_resistor_3 (.node(WSC));
  Pull_Resistor pull_resistor_4 (.node(WSB));
  assign WSD = xor_1_out ? xor_1_out : 1'bz;  // Controlled_Buffer controlled_buffer_15
  assign WSC = xor_2_out ? xor_2_out : 1'bz;  // Controlled_Buffer controlled_buffer_16
  assign WSB = xor_3_out ? xor_3_out : 1'bz;  // Controlled_Buffer controlled_buffer_17
  ExactlyOne xor_1 (
    .out(xor_1_out), .in0(groupinglogic_1_iload[11]), .in1(groupinglogic_1_iload[10]),
    .in2(groupinglogic_1_iload[9]));
  ExactlyOne xor_2 (
    .out(xor_2_out), .in0(groupinglogic_1_iload[8]), .in1(groupinglogic_1_iload[7]),
    .in2(groupinglogic_1_iload[6]));
  ExactlyOne xor_3 (
    .out(xor_3_out), .in0(groupinglogic_1_iload[5]), .in1(groupinglogic_1_iload[4]),
    .in2(groupinglogic_1_iload[3]));
  not not_2 (not_2_out, DIN_ENB);
  xor xor_4 (xor_4_out, not_2_out, PLR);
  assign RegCol_DIN = xor_4_out ? groupinglogic_1_x : 16'bz;  // Controlled_Buffer controlled_buffer_18
  assign RSA = PHR ? decoder_2_out0 : 1'bz;  // Controlled_Buffer controlled_buffer_19
  assign RSB = PHR ? decoder_2_out1 : 1'bz;  // Controlled_Buffer controlled_buffer_20
  assign RSC = PHR ? decoder_2_out2 : 1'bz;  // Controlled_Buffer controlled_buffer_21
  assign RSD = PHR ? decoder_2_out3 : 1'bz;  // Controlled_Buffer controlled_buffer_22
  assign RIP = PHR ? decoder_2_out4 : 1'bz;  // Controlled_Buffer controlled_buffer_23
  Pull_Resistor pull_resistor_5 (.node(RIP));
  xor xor_5 (REG_ENABLE, xor_6_out, xor_7_out);
  ExactlyOne xor_6 (.out(xor_6_out), .in0(RSD), .in1(RSC), .in2(RSB), .in3(RSA));
  ExactlyOne xor_7 (.out(xor_7_out), .in0(WSD), .in1(WSC), .in2(WSB), .in3(WSA));
  assign controlled_buffer_13_out = RSC ? 3'b010 : 3'bz;  // Controlled_Buffer controlled_buffer_24
  assign controlled_buffer_25_out = WSC ? 3'b010 : 3'bz;  // Controlled_Buffer controlled_buffer_25
  assign controlled_buffer_13_out = RSD ? 3'b011 : 3'bz;  // Controlled_Buffer controlled_buffer_26
  assign controlled_buffer_25_out = WSD ? 3'b011 : 3'bz;  // Controlled_Buffer controlled_buffer_27
  RegCol regcol_1 (
    .ENBL(REG_ENABLE), .RX(RSX), .RH(RSH), .RL(RSL), .WX(WSX), .WH(WSH), .WL(WSL), .CLK(CLK),
    .RSEL(controlled_buffer_13_out), .WSEL(controlled_buffer_25_out), .DIN(RegCol_DIN), .DOUT(regcol_1_dout));
  Pull_Resistor pull_resistor_6 (.node(WSX));
  assign WSX = xor_8_out ? xor_8_out : 1'bz;  // Controlled_Buffer controlled_buffer_28
  ExactlyOne xor_8 (
    .out(xor_8_out), .in0(groupinglogic_1_iload[9]), .in1(groupinglogic_1_iload[6]),
    .in2(groupinglogic_1_iload[3]), .in3(groupinglogic_1_iload[0]));
  Pull_Resistor pull_resistor_7 (.node(WSA));
  assign WSA = xor_9_out ? xor_9_out : 1'bz;  // Controlled_Buffer controlled_buffer_29
  ExactlyOne xor_9 (
    .out(xor_9_out), .in0(groupinglogic_1_iload[2]), .in1(groupinglogic_1_iload[1]),
    .in2(groupinglogic_1_iload[0]));
  Pull_Resistor pull_resistor_8 (.node(RAM_ADDRIN_ENBL));
  Bit_Extender #(.out_width(3), .\type ("zero")) bit_extender_4 (.in(HI8), .out(bit_extender_4_out));
  Decoder #(.enable("false"), .select(3)) decoder_2 (
    .out0(decoder_2_out0), .out1(decoder_2_out1), .out2(decoder_2_out2), .out3(decoder_2_out3),
    .out4(decoder_2_out4), .sel(bit_extender_4_out));  // open: out5, out6, out7
  assign controlled_buffer_25_out = WSA ? 3'b000 : 3'bz;  // Controlled_Buffer controlled_buffer_30
  assign controlled_buffer_25_out = WSB ? 3'b001 : 3'bz;  // Controlled_Buffer controlled_buffer_31
  ExactlyOne xor_10 (.out(xor_10_out), .in0(RSX), .in1(RSH), .in2(RSL));
  Pull_Resistor pull_resistor_9 (.node(WSH));
  assign WSH = xor_11_out ? xor_11_out : 1'bz;  // Controlled_Buffer controlled_buffer_32
  ExactlyOne xor_11 (
    .out(xor_11_out), .in0(groupinglogic_1_iload[10]), .in1(groupinglogic_1_iload[7]),
    .in2(groupinglogic_1_iload[4]), .in3(groupinglogic_1_iload[1]));
  not not_3 (not_3_out, RIP);
  Pull_Resistor pull_resistor_10 (.node(RegCol_Enb));
  assign RegCol_Enb = not_3_out ? xor_10_out : 1'bz;  // Controlled_Buffer controlled_buffer_33
  Pull_Resistor pull_resistor_11 (.node(WSL));
  assign WSL = xor_12_out ? xor_12_out : 1'bz;  // Controlled_Buffer controlled_buffer_34
  ExactlyOne xor_12 (
    .out(xor_12_out), .in0(groupinglogic_1_iload[11]), .in1(groupinglogic_1_iload[8]),
    .in2(groupinglogic_1_iload[5]), .in3(groupinglogic_1_iload[2]));
  // Probe on regcol_1_dout
  assign controlled_buffer_35_out = xor_13_out ? X16 : 16'bz;  // Controlled_Buffer controlled_buffer_35
  assign controlled_buffer_36_out = LDSP ? HI8 : 8'bz;  // Controlled_Buffer controlled_buffer_36
  assign controlled_buffer_37_out = RAM_ADDRIN_ENBL ? RAM_Addr : 16'bz;  // Controlled_Buffer controlled_buffer_37
  DEL_NOT16 del_not16_1 (.D(CLK), .Q(del_not16_1_q));
  assign RegCol_Out = regcol_1_dout;  // Buffer buffer_1, 16 bits wide
  xor xor_13 (xor_13_out, PHR, PHI);
  // Stack256 stack256_1: pin names not known; wires that end beside it: xor_13_out, controlled_buffer_35_out, DESP, SRST, controlled_buffer_36_out, CLK, LDSP, stack256_1_p8, stack256_1_p9, stack256_1_p10
  assign controlled_buffer_37_out = STACK_INSTR ? stack256_1_p8 : 16'bz;  // Controlled_Buffer controlled_buffer_38
  RAM #(.addrWidth(16), .dataWidth(16), .enables("line")) ram_1 (
    .addr(controlled_buffer_37_out), .we(or_1_out), .clk(del_not16_2_q), .din(RAM_VAL), .dout(ram_1_dout));
  or or_1 (or_1_out, stack256_1_p9, RegCol_Enb);
  DEL_NOT16 del_not16_2 (.D(del_not16_1_q), .Q(del_not16_2_q));
  assign RAM_VAL = RegCol_Enb ? RegCol_Out : 16'bz;  // Controlled_Buffer controlled_buffer_39
  xor xor_14 (xor_14_out, PHI, RIP);
  assign RAM_VAL = xor_14_out ? stack256_1_p10 : 16'bz;  // Controlled_Buffer controlled_buffer_40
  Pull_Resistor pull_resistor_12 (.node(WSD));
  Pull_Resistor pull_resistor_13 (.node(WSC));
  Pull_Resistor pull_resistor_14 (.node(WSB));
  assign WSD = xor_15_out ? xor_15_out : 1'bz;  // Controlled_Buffer controlled_buffer_41
  assign WSC = xor_16_out ? xor_16_out : 1'bz;  // Controlled_Buffer controlled_buffer_42
  assign WSB = xor_17_out ? xor_17_out : 1'bz;  // Controlled_Buffer controlled_buffer_43
  ExactlyOne xor_15 (
    .out(xor_15_out), .in0(groupinglogic_1_rload[11]), .in1(groupinglogic_1_rload[10]),
    .in2(groupinglogic_1_rload[9]));
  ExactlyOne xor_16 (
    .out(xor_16_out), .in0(groupinglogic_1_rload[8]), .in1(groupinglogic_1_rload[7]),
    .in2(groupinglogic_1_rload[6]));
  ExactlyOne xor_17 (
    .out(xor_17_out), .in0(groupinglogic_1_rload[5]), .in1(groupinglogic_1_rload[4]),
    .in2(groupinglogic_1_rload[3]));
  Pull_Resistor pull_resistor_15 (.node(WSX));
  assign WSX = xor_18_out ? xor_18_out : 1'bz;  // Controlled_Buffer controlled_buffer_44
  ExactlyOne xor_18 (
    .out(xor_18_out), .in0(groupinglogic_1_rload[9]), .in1(groupinglogic_1_rload[6]),
    .in2(groupinglogic_1_rload[3]), .in3(groupinglogic_1_rload[0]));
  Pull_Resistor pull_resistor_16 (.node(WSA));
  assign WSA = xor_19_out ? xor_19_out : 1'bz;  // Controlled_Buffer controlled_buffer_45
  ExactlyOne xor_19 (
    .out(xor_19_out), .in0(groupinglogic_1_rload[2]), .in1(groupinglogic_1_rload[1]),
    .in2(groupinglogic_1_rload[0]));
  Pull_Resistor pull_resistor_17 (.node(WSH));
  assign WSH = xor_20_out ? xor_20_out : 1'bz;  // Controlled_Buffer controlled_buffer_46
  ExactlyOne xor_20 (
    .out(xor_20_out), .in0(groupinglogic_1_rload[10]), .in1(groupinglogic_1_rload[7]),
    .in2(groupinglogic_1_rload[4]), .in3(groupinglogic_1_rload[1]));
  xor xor_21 (xor_21_out, PLR, DIN_ENB);
  assign RAM_ADDRIN_ENBL = DIN_ENB ? DIN_ENB : 1'bz;  // Controlled_Buffer controlled_buffer_47
  ExactlyOne xor_22 (.out(DIN_ENB), .in0(xor_18_out), .in1(xor_20_out), .in2(xor_23_out));
  Pull_Resistor pull_resistor_18 (.node(WSL));
  assign WSL = xor_23_out ? xor_23_out : 1'bz;  // Controlled_Buffer controlled_buffer_48
  ExactlyOne xor_23 (
    .out(xor_23_out), .in0(groupinglogic_1_rload[11]), .in1(groupinglogic_1_rload[8]),
    .in2(groupinglogic_1_rload[5]), .in3(groupinglogic_1_rload[2]));
  assign RegCol_DIN = xor_21_out ? ram_1_dout : 16'bz;  // Controlled_Buffer controlled_buffer_49
  Pull_Resistor pull_resistor_19 (.node(RSD));
  Pull_Resistor pull_resistor_20 (.node(RSC));
  Pull_Resistor pull_resistor_21 (.node(RSB));
  assign RSD = xor_24_out ? xor_24_out : 1'bz;  // Controlled_Buffer controlled_buffer_50
  assign RSC = xor_25_out ? xor_25_out : 1'bz;  // Controlled_Buffer controlled_buffer_51
  assign RSB = xor_26_out ? xor_26_out : 1'bz;  // Controlled_Buffer controlled_buffer_52
  ExactlyOne xor_24 (
    .out(xor_24_out), .in0(groupinglogic_1_store[11]), .in1(groupinglogic_1_store[10]),
    .in2(groupinglogic_1_store[9]));
  ExactlyOne xor_25 (
    .out(xor_25_out), .in0(groupinglogic_1_store[8]), .in1(groupinglogic_1_store[7]),
    .in2(groupinglogic_1_store[6]));
  ExactlyOne xor_26 (
    .out(xor_26_out), .in0(groupinglogic_1_store[5]), .in1(groupinglogic_1_store[4]),
    .in2(groupinglogic_1_store[3]));
  Pull_Resistor pull_resistor_22 (.node(RSX));
  assign RSX = xor_27_out ? xor_27_out : 1'bz;  // Controlled_Buffer controlled_buffer_53
  ExactlyOne xor_27 (
    .out(xor_27_out), .in0(groupinglogic_1_store[9]), .in1(groupinglogic_1_store[6]),
    .in2(groupinglogic_1_store[3]), .in3(groupinglogic_1_store[0]));
  Pull_Resistor pull_resistor_23 (.node(RSA));
  assign RSA = xor_28_out ? xor_28_out : 1'bz;  // Controlled_Buffer controlled_buffer_54
  ExactlyOne xor_28 (
    .out(xor_28_out), .in0(groupinglogic_1_store[2]), .in1(groupinglogic_1_store[1]),
    .in2(groupinglogic_1_store[0]));
  ExactlyOne xor_29 (.out(xor_29_out), .in0(xor_27_out), .in1(xor_30_out), .in2(xor_31_out));
  Pull_Resistor pull_resistor_24 (.node(RSH));
  assign RSH = xor_30_out ? xor_30_out : 1'bz;  // Controlled_Buffer controlled_buffer_55
  ExactlyOne xor_30 (
    .out(xor_30_out), .in0(groupinglogic_1_store[10]), .in1(groupinglogic_1_store[7]),
    .in2(groupinglogic_1_store[4]), .in3(groupinglogic_1_store[1]));
  assign RAM_ADDRIN_ENBL = xor_29_out ? xor_29_out : 1'bz;  // Controlled_Buffer controlled_buffer_56
  Pull_Resistor pull_resistor_25 (.node(RSL));
  assign RSL = xor_31_out ? xor_31_out : 1'bz;  // Controlled_Buffer controlled_buffer_57
  ExactlyOne xor_31 (
    .out(xor_31_out), .in0(groupinglogic_1_store[11]), .in1(groupinglogic_1_store[8]),
    .in2(groupinglogic_1_store[5]), .in3(groupinglogic_1_store[2]));
  Pull_Resistor pull_resistor_26 (.node(STACK_INSTR));
  assign STACK_INSTR = XOR_RAM_STACK_REQ_out ? XOR_RAM_STACK_REQ_out : 1'bz;  // Controlled_Buffer controlled_buffer_58
  ExactlyOne XOR_RAM_STACK_REQ (
    .out(XOR_RAM_STACK_REQ_out), .in0(groupinglogic_1_stack[1]), .in1(groupinglogic_1_stack[2]),
    .in2(groupinglogic_1_stack[3]), .in3(groupinglogic_1_stack[4]), .in4(groupinglogic_1_stack[5]),
    .in5(groupinglogic_1_stack[6]));
  Pull_Resistor pull_resistor_27 (.node(DESP));
  assign DESP = groupinglogic_1_stack[9] ? groupinglogic_1_stack[9] : 1'bz;  // Controlled_Buffer controlled_buffer_59
  Pull_Resistor pull_resistor_28 (.node(RDSP));
  assign RDSP = groupinglogic_1_stack[8] ? groupinglogic_1_stack[8] : 1'bz;  // Controlled_Buffer controlled_buffer_60
  Pull_Resistor pull_resistor_29 (.node(LDSP));
  assign LDSP = groupinglogic_1_stack[7] ? groupinglogic_1_stack[7] : 1'bz;  // Controlled_Buffer controlled_buffer_61
  Pull_Resistor pull_resistor_30 (.node(JSR));
  assign JSR = groupinglogic_1_stack[6] ? groupinglogic_1_stack[6] : 1'bz;  // Controlled_Buffer controlled_buffer_62
  Pull_Resistor pull_resistor_31 (.node(PLR));
  assign PLR = groupinglogic_1_stack[5] ? groupinglogic_1_stack[5] : 1'bz;  // Controlled_Buffer controlled_buffer_63
  Pull_Resistor pull_resistor_32 (.node(RFI));
  assign RFI = groupinglogic_1_stack[4] ? groupinglogic_1_stack[4] : 1'bz;  // Controlled_Buffer controlled_buffer_64
  Pull_Resistor pull_resistor_33 (.node(RFS));
  assign RFS = groupinglogic_1_stack[3] ? groupinglogic_1_stack[3] : 1'bz;  // Controlled_Buffer controlled_buffer_65
  Pull_Resistor pull_resistor_34 (.node(PHR));
  assign PHR = groupinglogic_1_stack[2] ? groupinglogic_1_stack[2] : 1'bz;  // Controlled_Buffer controlled_buffer_66
  Pull_Resistor pull_resistor_35 (.node(PHI));
  assign PHI = groupinglogic_1_stack[1] ? groupinglogic_1_stack[1] : 1'bz;  // Controlled_Buffer controlled_buffer_67
  Pull_Resistor pull_resistor_36 (.node(SRST));
  assign SRST = groupinglogic_1_stack[0] ? groupinglogic_1_stack[0] : 1'bz;  // Controlled_Buffer controlled_buffer_68

  // Other names for the same wires on the sheet: WIP = JMP

  // Notes on the sheet:
  //   contents of rom_1 (hex, n*v repeats v):
  //   bf0000 800000 ffff bf0000 810fff bf0000 820000 bf0000 81caca bf0000 850000 bf0000 890000 bf0000
  //   820004 bf0000 bf0000 bf0000 850004 65517*bf0000
endmodule

module RegCol (
  input  CLK,
  input  [2:0] RSEL,
  input  [2:0] WSEL,
  input  [15:0] DIN,
  input  ENBL,
  input  RX,
  input  RH,
  input  RL,
  input  WX,
  input  WH,
  input  WL,
  output [15:0] DOUT
);

  wire and_1_out, and_2_out, and_3_out, and_4_out, and_5_out, and_6_out, and_7_out, and_8_out, and_9_out,
       and_10_out, and_11_out, and_12_out, demultiplexer_1_out0, demultiplexer_1_out1, demultiplexer_1_out2,
       demultiplexer_1_out3, demultiplexer_2_out0, demultiplexer_2_out1, demultiplexer_2_out2,
       demultiplexer_2_out3;
  wire [15:0] RA_qh, RA_ql, RA_qx, RB_qh, RB_ql, RB_qx, RC_qh, RC_ql, RC_qx, RD_qh, RD_ql, RD_qx;

  Demultiplexer #(.select(3)) demultiplexer_1 (
    .out0(demultiplexer_1_out0), .out1(demultiplexer_1_out1), .out2(demultiplexer_1_out2),
    .out3(demultiplexer_1_out3), .in(ENBL), .sel(RSEL));  // open: out4, out5, out6, out7
  Reg16 RA (
    .D(DIN), .WH(WH), .WL(WL), .CLK(CLK), .WE(demultiplexer_2_out0), .WX(WX), .RE(demultiplexer_1_out0),
    .RL(RL), .RH(RH), .RX(RX), .QH(RA_qh), .QX(RA_qx), .QL(RA_ql));
  Reg16 RB (
    .D(DIN), .WH(WH), .WL(WL), .CLK(CLK), .WE(demultiplexer_2_out1), .WX(WX), .RE(demultiplexer_1_out1),
    .RL(RL), .RH(RH), .RX(RX), .QH(RB_qh), .QX(RB_qx), .QL(RB_ql));
  Reg16 RC (
    .D(DIN), .WH(WH), .WL(WL), .CLK(CLK), .WE(demultiplexer_2_out2), .WX(WX), .RE(demultiplexer_1_out2),
    .RL(RL), .RH(RH), .RX(RX), .QH(RC_qh), .QX(RC_qx), .QL(RC_ql));
  Reg16 RD (
    .D(DIN), .WH(WH), .WL(WL), .CLK(CLK), .WE(demultiplexer_2_out3), .WX(WX), .RE(demultiplexer_1_out3),
    .RL(RL), .RH(RH), .RX(RX), .QH(RD_qh), .QX(RD_qx), .QL(RD_ql));
  Demultiplexer #(.select(3)) demultiplexer_2 (
    .out0(demultiplexer_2_out0), .out1(demultiplexer_2_out1), .out2(demultiplexer_2_out2),
    .out3(demultiplexer_2_out3), .in(ENBL), .sel(WSEL));  // open: out4, out5, out6, out7
  and and_1 (and_1_out, demultiplexer_1_out0, RH);
  assign DOUT = and_1_out ? RA_qh : 16'bz;  // Controlled_Buffer controlled_buffer_1
  and and_2 (and_2_out, demultiplexer_1_out0, RX);
  assign DOUT = and_2_out ? RA_qx : 16'bz;  // Controlled_Buffer controlled_buffer_2
  and and_3 (and_3_out, demultiplexer_1_out1, RH);
  assign DOUT = and_3_out ? RB_qh : 16'bz;  // Controlled_Buffer controlled_buffer_3
  and and_4 (and_4_out, demultiplexer_1_out1, RX);
  assign DOUT = and_4_out ? RB_qx : 16'bz;  // Controlled_Buffer controlled_buffer_4
  and and_5 (and_5_out, demultiplexer_1_out2, RH);
  assign DOUT = and_5_out ? RC_qh : 16'bz;  // Controlled_Buffer controlled_buffer_5
  and and_6 (and_6_out, demultiplexer_1_out2, RX);
  assign DOUT = and_6_out ? RC_qx : 16'bz;  // Controlled_Buffer controlled_buffer_6
  and and_7 (and_7_out, demultiplexer_1_out3, RH);
  assign DOUT = and_7_out ? RD_qh : 16'bz;  // Controlled_Buffer controlled_buffer_7
  and and_8 (and_8_out, demultiplexer_1_out3, RX);
  assign DOUT = and_8_out ? RD_qx : 16'bz;  // Controlled_Buffer controlled_buffer_8
  and and_9 (and_9_out, demultiplexer_1_out0, RL);
  assign DOUT = and_9_out ? RA_ql : 16'bz;  // Controlled_Buffer controlled_buffer_9
  and and_10 (and_10_out, demultiplexer_1_out1, RL);
  assign DOUT = and_10_out ? RB_ql : 16'bz;  // Controlled_Buffer controlled_buffer_10
  and and_11 (and_11_out, demultiplexer_1_out2, RL);
  assign DOUT = and_11_out ? RC_ql : 16'bz;  // Controlled_Buffer controlled_buffer_11
  and and_12 (and_12_out, demultiplexer_1_out3, RL);
  assign DOUT = and_12_out ? RD_ql : 16'bz;  // Controlled_Buffer controlled_buffer_12
endmodule

module Reg16 (
  input  RE,
  input  WE,
  input  RH,
  input  WX,
  input  RX,
  input  WH,
  input  RL,
  input  WL,
  input  CLK,
  input  [15:0] D,
  output [15:0] QH,
  output [15:0] QX,
  output [15:0] QL
);

  wire and_1_out, and_2_out, and_3_out, and_4_out, and_5_out, or_1_out, or_2_out;
  wire [7:0] AH_q, AL_q, controlled_buffer_2_out, pull_resistor_1_node;

  or or_1 (or_1_out, WX, WH);
  or or_2 (or_2_out, WX, WL);
  Register AH (.D(D[15:8]), .en(and_1_out), .clk(CLK), .Q(AH_q));  // open: clr
  and and_1 (and_1_out, WE, or_1_out);
  Register AL (.D(D[7:0]), .en(and_2_out), .clk(CLK), .Q(AL_q));  // open: clr
  and and_2 (and_2_out, WE, or_2_out);
  and and_3 (and_3_out, RX, RE);
  assign QX = and_3_out ? {AL_q, AH_q} : 16'bz;  // Controlled_Buffer controlled_buffer_1
  and and_4 (and_4_out, RL, RE);
  assign controlled_buffer_2_out = and_4_out ? AL_q : 8'bz;  // Controlled_Buffer controlled_buffer_2
  and and_5 (and_5_out, RH, RE);
  Pull_Resistor pull_resistor_1 (.node(pull_resistor_1_node));
  assign QH = {{8{1'b0}}, pull_resistor_1_node};  // Bit_Extender bit_extender_1
  assign pull_resistor_1_node = and_5_out ? AH_q : 8'bz;  // Controlled_Buffer controlled_buffer_3
  Pull_Resistor pull_resistor_2 (.node(QX));
  Pull_Resistor pull_resistor_3 (.node(controlled_buffer_2_out));
  assign QL = {{8{1'b0}}, controlled_buffer_2_out};  // Bit_Extender bit_extender_2
endmodule

module IP (
  input  JMP,
  input  CLK,
  input  [15:0] JMPLOC,
  output [15:0] IPOUT
);

  wire comparator_1_eq, comparator_1_lt, controlled_buffer_3_out, not_1_out, rgbled_1_p2, xor_1_out;
  wire [15:0] controlled_buffer_1_out, counter_1_q;

  // RGBLED rgbled_1: pin names not known; wires that end beside it: JMP, rgbled_1_p2, CLK
  assign controlled_buffer_1_out = JMP ? JMPLOC : 16'bz;  // Controlled_Buffer controlled_buffer_1
  assign controlled_buffer_1_out = rgbled_1_p2 ? 16'hff00 : 16'bz;  // Controlled_Buffer controlled_buffer_2
  Counter #(.max('hffff), .width(16)) counter_1 (
    .load(controlled_buffer_3_out), .clk(CLK), .D(controlled_buffer_1_out), .Q(counter_1_q));  // open: clr, up, count, carry
  assign controlled_buffer_3_out = JMP ? JMP : 1'bz;  // Controlled_Buffer controlled_buffer_3
  assign controlled_buffer_3_out = rgbled_1_p2 ? rgbled_1_p2 : 1'bz;  // Controlled_Buffer controlled_buffer_4
  POR #(.PorHighDuration(1)) por_1 (.out(rgbled_1_p2));
  Comparator #(.mode("unsigned"), .width(16)) comparator_1 (
    .a(16'hfeff), .b(counter_1_q), .eq(comparator_1_eq), .lt(comparator_1_lt));  // open: gt
  assign IPOUT = xor_1_out ? counter_1_q : 16'bz;  // Controlled_Buffer controlled_buffer_5
  not not_1 (not_1_out, comparator_1_eq);
  xor xor_1 (xor_1_out, not_1_out, comparator_1_lt);

  // Notes on the sheet:
  //   Reset Vector
endmodule

module InstructionParser (
  input  [23:0] Instruction,
  output Cat0,
  output [2:0] Category,
  output [4:0] Subinstruction,
  output [7:0] OperandHigh,
  output [7:0] OperandLow,
  output [15:0] OperandFull
);

  nor nor_1 (Cat0, Instruction[23], Instruction[22], Instruction[21]);
  LED NorCat (.in(Cat0));
  LED Si_Bit0 (.in(Instruction[16]));
  LED Si_Bit1 (.in(Instruction[17]));
  LED Si_Bit2 (.in(Instruction[18]));
  LED Si_Bit3 (.in(Instruction[19]));
  LED Si_Bit4 (.in(Instruction[20]));
  // RGBLED CategoryLED: pin names not known; wires that end beside it: Instruction[23], Instruction[22], Instruction[21]

  assign Category = Instruction[23:21];
  assign OperandFull = Instruction[15:0];
  assign OperandHigh = Instruction[15:8];
  assign OperandLow = Instruction[7:0];
  assign Subinstruction = Instruction[20:16];
endmodule

module SplittingLogic (
  input  [23:0] ROM_IN,
  output [15:0] OperandX,
  output [7:0] OperandLo,
  output Cat_0,
  output Cat_1,
  output [7:0] OperandHi,
  output Cat_2,
  output Cat_3,
  output Cat_4,
  output Cat_5,
  output Cat_6,
  output Cat_7,
  output i0,
  output i1,
  output i2,
  output i3,
  output i4,
  output i5,
  output i6,
  output i7,
  output i8,
  output i9,
  output i10,
  output i11,
  output i12,
  output i13,
  output i14,
  output i15,
  output i16,
  output i17,
  output i18,
  output i19,
  output i20,
  output i21,
  output i22,
  output i23,
  output i24,
  output i25,
  output i26,
  output i27,
  output i28,
  output i29,
  output i30,
  output i31
);

  wire [2:0] Parser_category;
  wire [4:0] Parser_subinstruction;

  Decoder #(.enable("false"), .select(3)) decoder_1 (
    .out0(Cat_0), .out1(Cat_1), .out2(Cat_2), .out3(Cat_3), .out4(Cat_4), .out5(Cat_5), .out6(Cat_6),
    .out7(Cat_7), .sel(Parser_category));
  Decoder #(.enable("false"), .select(5)) decoder_2 (
    .out0(i0), .out1(i1), .out2(i2), .out3(i3), .out4(i4), .out5(i5), .out6(i6), .out7(i7), .out8(i8),
    .out9(i9), .out10(i10), .out11(i11), .out12(i12), .out13(i13), .out14(i14), .out15(i15), .out16(i16),
    .out17(i17), .out18(i18), .out19(i19), .out20(i20), .out21(i21), .out22(i22), .out23(i23), .out24(i24),
    .out25(i25), .out26(i26), .out27(i27), .out28(i28), .out29(i29), .out30(i30), .out31(i31),
    .sel(Parser_subinstruction));
  // Probe on ROM_IN
  InstructionParser Parser (
    .Instruction(ROM_IN), .Category(Parser_category), .Subinstruction(Parser_subinstruction),
    .OperandHigh(OperandHi), .OperandLow(OperandLo), .OperandFull(OperandX));  // open: Cat0
endmodule

module GroupingLogic (
  input  [23:0] Instruction,
  output [7:0] HI,
  output [7:0] LO,
  output [15:0] X,
  output [31:0] ILOAD,
  output [31:0] RLOAD,
  output [31:0] STORE,
  output [31:0] ALU,
  output [31:0] STACK,
  output [31:0] MISC,
  output [31:0] RESERVED1,
  output [31:0] RESERVED2
);

  wire splittinglogic_1_cat_0, splittinglogic_1_cat_1, splittinglogic_1_cat_2, splittinglogic_1_cat_3,
       splittinglogic_1_cat_4, splittinglogic_1_cat_5, splittinglogic_1_cat_6, splittinglogic_1_cat_7;
  wire [31:0] splittinglogic_1_i0;

  SplittingLogic splittinglogic_1 (
    .ROM_IN(Instruction), .Cat_1(splittinglogic_1_cat_1), .Cat_7(splittinglogic_1_cat_7),
    .Cat_2(splittinglogic_1_cat_2), .Cat_6(splittinglogic_1_cat_6), .Cat_3(splittinglogic_1_cat_3),
    .Cat_5(splittinglogic_1_cat_5), .i1(splittinglogic_1_i0[1]), .i3(splittinglogic_1_i0[3]),
    .i5(splittinglogic_1_i0[5]), .i7(splittinglogic_1_i0[7]), .i9(splittinglogic_1_i0[9]),
    .i11(splittinglogic_1_i0[11]), .i13(splittinglogic_1_i0[13]), .i15(splittinglogic_1_i0[15]),
    .i17(splittinglogic_1_i0[17]), .i19(splittinglogic_1_i0[19]), .i21(splittinglogic_1_i0[21]),
    .i23(splittinglogic_1_i0[23]), .i25(splittinglogic_1_i0[25]), .i27(splittinglogic_1_i0[27]),
    .i29(splittinglogic_1_i0[29]), .i31(splittinglogic_1_i0[31]), .Cat_4(splittinglogic_1_cat_4),
    .i0(splittinglogic_1_i0[0]), .i2(splittinglogic_1_i0[2]), .i4(splittinglogic_1_i0[4]),
    .i6(splittinglogic_1_i0[6]), .i8(splittinglogic_1_i0[8]), .i10(splittinglogic_1_i0[10]),
    .i12(splittinglogic_1_i0[12]), .i14(splittinglogic_1_i0[14]), .i16(splittinglogic_1_i0[16]),
    .i18(splittinglogic_1_i0[18]), .i20(splittinglogic_1_i0[20]), .i22(splittinglogic_1_i0[22]),
    .i24(splittinglogic_1_i0[24]), .i26(splittinglogic_1_i0[26]), .i28(splittinglogic_1_i0[28]),
    .i30(splittinglogic_1_i0[30]), .OperandHi(HI), .OperandLo(LO), .OperandX(X),
    .Cat_0(splittinglogic_1_cat_0));
  Pull_Resistor pull_resistor_1 (.node(ILOAD));
  assign ILOAD = splittinglogic_1_cat_0 ? splittinglogic_1_i0 : 32'bz;  // Controlled_Buffer controlled_buffer_1
  Pull_Resistor pull_resistor_2 (.node(RLOAD));
  assign RLOAD = splittinglogic_1_cat_1 ? splittinglogic_1_i0 : 32'bz;  // Controlled_Buffer controlled_buffer_2
  Pull_Resistor pull_resistor_3 (.node(STORE));
  assign STORE = splittinglogic_1_cat_2 ? splittinglogic_1_i0 : 32'bz;  // Controlled_Buffer controlled_buffer_3
  Pull_Resistor pull_resistor_4 (.node(ALU));
  assign ALU = splittinglogic_1_cat_3 ? splittinglogic_1_i0 : 32'bz;  // Controlled_Buffer controlled_buffer_4
  Pull_Resistor pull_resistor_5 (.node(STACK));
  assign STACK = splittinglogic_1_cat_4 ? splittinglogic_1_i0 : 32'bz;  // Controlled_Buffer controlled_buffer_5
  Pull_Resistor pull_resistor_6 (.node(MISC));
  assign MISC = splittinglogic_1_cat_5 ? splittinglogic_1_i0 : 32'bz;  // Controlled_Buffer controlled_buffer_6
  Pull_Resistor pull_resistor_7 (.node(RESERVED1));
  assign RESERVED1 = splittinglogic_1_cat_6 ? splittinglogic_1_i0 : 32'bz;  // Controlled_Buffer controlled_buffer_7
  Pull_Resistor pull_resistor_8 (.node(RESERVED2));
  assign RESERVED2 = splittinglogic_1_cat_7 ? splittinglogic_1_i0 : 32'bz;  // Controlled_Buffer controlled_buffer_8
  LED ILOAD_LED (.in(splittinglogic_1_cat_0));
  LED RLOAD_LED (.in(splittinglogic_1_cat_1));
  LED STORE_LED (.in(splittinglogic_1_cat_2));
  LED ALU_LED (.in(splittinglogic_1_cat_3));
  LED STACK_LED (.in(splittinglogic_1_cat_4));
  LED MISC_LED (.in(splittinglogic_1_cat_5));
endmodule

module PositiveFuse (
  input  SET,
  output Q
);

  wire por_1_out, s_r_ff_1_qn;

  S_R_Flip_Flop s_r_ff_1 (.clk(SET), .Q(Q), .reset(por_1_out), .Qn(s_r_ff_1_qn), .preset(SET));  // open: S, R
  LED FUSED (.in(Q));
  LED UNFUSED (.in(s_r_ff_1_qn));
  POR #(.PorHighDuration(1)) por_1 (.out(por_1_out));
endmodule

module test (
  input  POP,
  input  PUSH,
  input  [15:0] PUSH_VAL,
  input  LDSP,
  input  [7:0] SI,
  input  INIT,
  output [15:0] RAM_ADDR,
  output RAM_WE,
  output [15:0] RAM_VAL,
  output [15:0] POP_VAL,
  output [15:0] SPOUT
);

  wire clock_1_out, controlled_buffer_1_out, controlled_buffer_4_out, counter_1_carry, del_not16_1_q,
       del_not16_2_q, nor_1_out, pull_resistor_1_node, splittinglogic_1_cat_0, splittinglogic_1_cat_1,
       splittinglogic_1_cat_2, splittinglogic_1_cat_3, splittinglogic_1_cat_4, splittinglogic_1_cat_5,
       splittinglogic_1_cat_6, splittinglogic_1_cat_7, splittinglogic_1_i0, splittinglogic_1_i1,
       splittinglogic_1_i2, splittinglogic_1_i3, splittinglogic_1_i4, splittinglogic_1_i5,
       splittinglogic_1_i6, splittinglogic_1_i7, splittinglogic_1_i8, splittinglogic_1_i9,
       splittinglogic_1_i10, splittinglogic_1_i11, splittinglogic_1_i12, splittinglogic_1_i13,
       splittinglogic_1_i14, splittinglogic_1_i15, splittinglogic_1_i16, splittinglogic_1_i17,
       splittinglogic_1_i18, splittinglogic_1_i19, splittinglogic_1_i20, splittinglogic_1_i21,
       splittinglogic_1_i22, splittinglogic_1_i23, splittinglogic_1_i24, splittinglogic_1_i25,
       splittinglogic_1_i26, splittinglogic_1_i27, splittinglogic_1_i28, splittinglogic_1_i29,
       splittinglogic_1_i30, splittinglogic_1_i31, xor_1_out;
  wire [7:0] controlled_buffer_2_out, undriven, undriven_2;
  wire [23:16] counter_1_q;

  Counter #(.max('h1f), .width(5)) counter_1 (
    .clk(clock_1_out), .carry(counter_1_carry), .Q(counter_1_q[20:16]));  // open: clr, load, up, count, D
  Clock clock_1 (.out(clock_1_out));
  assign controlled_buffer_1_out = LDSP ? LDSP : 1'bz;  // Controlled_Buffer controlled_buffer_1
  assign controlled_buffer_2_out = LDSP ? SI : 8'bz;  // Controlled_Buffer controlled_buffer_2
  Counter #(.max('h7), .width(3)) counter_2 (
    .clk(counter_1_carry), .Q(counter_1_q[23:21]));  // open: clr, load, up, count, D, carry
  DEL_NOT16 del_not16_1 (.D(POP), .Q(del_not16_1_q));
  DEL_NOT16 del_not16_2 (.D(del_not16_1_q), .Q(del_not16_2_q));
  assign controlled_buffer_1_out = INIT ? INIT : 1'bz;  // Controlled_Buffer controlled_buffer_3
  nor nor_1 (nor_1_out, ~PUSH, del_not16_2_q);  // NOR_Gate
  assign controlled_buffer_4_out = nor_1_out ? nor_1_out : 1'bz;  // Controlled_Buffer controlled_buffer_4
  Pull_Resistor pull_resistor_1 (.node(pull_resistor_1_node));
  xor xor_1 (xor_1_out, del_not16_2_q, PUSH);
  assign pull_resistor_1_node = xor_1_out ? xor_1_out : 1'bz;  // Controlled_Buffer controlled_buffer_5
  Pull_Resistor pull_resistor_2 ();  // open: node
  Pull_Resistor pull_resistor_3 (.node(controlled_buffer_1_out));
  assign controlled_buffer_2_out = INIT ? {8{1'b0}} : 8'bz;  // Controlled_Buffer controlled_buffer_6
  SplittingLogic splittinglogic_1 (
    .ROM_IN({counter_1_q, undriven_2, undriven}), .Cat_1(splittinglogic_1_cat_1),
    .Cat_7(splittinglogic_1_cat_7), .Cat_2(splittinglogic_1_cat_2), .Cat_6(splittinglogic_1_cat_6),
    .Cat_3(splittinglogic_1_cat_3), .Cat_5(splittinglogic_1_cat_5), .i1(splittinglogic_1_i1),
    .i3(splittinglogic_1_i3), .i5(splittinglogic_1_i5), .i7(splittinglogic_1_i7), .i9(splittinglogic_1_i9),
    .i11(splittinglogic_1_i11), .i13(splittinglogic_1_i13), .i15(splittinglogic_1_i15),
    .i17(splittinglogic_1_i17), .i19(splittinglogic_1_i19), .i21(splittinglogic_1_i21),
    .i23(splittinglogic_1_i23), .i25(splittinglogic_1_i25), .i27(splittinglogic_1_i27),
    .i29(splittinglogic_1_i29), .i31(splittinglogic_1_i31), .Cat_4(splittinglogic_1_cat_4),
    .i0(splittinglogic_1_i0), .i2(splittinglogic_1_i2), .i4(splittinglogic_1_i4), .i6(splittinglogic_1_i6),
    .i8(splittinglogic_1_i8), .i10(splittinglogic_1_i10), .i12(splittinglogic_1_i12),
    .i14(splittinglogic_1_i14), .i16(splittinglogic_1_i16), .i18(splittinglogic_1_i18),
    .i20(splittinglogic_1_i20), .i22(splittinglogic_1_i22), .i24(splittinglogic_1_i24),
    .i26(splittinglogic_1_i26), .i28(splittinglogic_1_i28), .i30(splittinglogic_1_i30),
    .Cat_0(splittinglogic_1_cat_0));  // open: OperandHi, OperandLo, OperandX
  Counter #(.max('hfefe), .width(16)) counter_3 (
    .load(controlled_buffer_1_out), .up(controlled_buffer_4_out), .clk(pull_resistor_1_node),
    .D({8'hfe, controlled_buffer_2_out}), .Q(RAM_ADDR));  // open: clr, count, carry
  Pull_Resistor pull_resistor_4 (.node(controlled_buffer_4_out));
  assign controlled_buffer_4_out = controlled_buffer_1_out ? controlled_buffer_1_out : 1'bz;  // Controlled_Buffer controlled_buffer_7
  assign pull_resistor_1_node = controlled_buffer_1_out ? controlled_buffer_1_out : 1'bz;  // Controlled_Buffer controlled_buffer_8
  LedBar ledbar_1 (
    .led0(splittinglogic_1_cat_0), .led1(splittinglogic_1_cat_1), .led2(splittinglogic_1_cat_2),
    .led3(splittinglogic_1_cat_3), .led4(splittinglogic_1_cat_4), .led5(splittinglogic_1_cat_5),
    .led6(splittinglogic_1_cat_6), .led7(splittinglogic_1_cat_7));
  LedBar ledbar_2 (
    .led0(splittinglogic_1_i31), .led1(splittinglogic_1_i30), .led2(splittinglogic_1_i29),
    .led3(splittinglogic_1_i28), .led4(splittinglogic_1_i27), .led5(splittinglogic_1_i26),
    .led6(splittinglogic_1_i25), .led7(splittinglogic_1_i24));
  LedBar ledbar_3 (
    .led0(splittinglogic_1_i23), .led1(splittinglogic_1_i22), .led2(splittinglogic_1_i21),
    .led3(splittinglogic_1_i20), .led4(splittinglogic_1_i19), .led5(splittinglogic_1_i18),
    .led6(splittinglogic_1_i17), .led7(splittinglogic_1_i16));
  LedBar ledbar_4 (
    .led0(splittinglogic_1_i15), .led1(splittinglogic_1_i14), .led2(splittinglogic_1_i13),
    .led3(splittinglogic_1_i12), .led4(splittinglogic_1_i11), .led5(splittinglogic_1_i10),
    .led6(splittinglogic_1_i9), .led7(splittinglogic_1_i8));
  LedBar ledbar_5 (
    .led0(splittinglogic_1_i7), .led1(splittinglogic_1_i6), .led2(splittinglogic_1_i5),
    .led3(splittinglogic_1_i4), .led4(splittinglogic_1_i3), .led5(splittinglogic_1_i2),
    .led6(splittinglogic_1_i1), .led7(splittinglogic_1_i0));

  assign RAM_VAL = PUSH_VAL;
  assign RAM_WE = PUSH;
  assign SPOUT = RAM_ADDR;

  // Notes on the sheet:
  //   TOP
endmodule

module NegativeFuse (
  input  SET,
  output Q
);

  wire s_r_ff_1_qn, undriven;

  S_R_Flip_Flop s_r_ff_1 (.clk(SET), .Q(Q), .reset(undriven), .Qn(s_r_ff_1_qn), .preset(SET));  // open: S, R
  LED FUSED (.in(Q));
  LED UNFUSED (.in(s_r_ff_1_qn));
endmodule

module latch (
  input  A,
  input  B,
  output D,
  output Q
);

  nor nor_1 (D, A, Q);
  nor nor_2 (Q, D, B);
endmodule

module Stack256 (
  input  POP,
  input  PUSH,
  input  [15:0] PUSH_VAL,
  input  LDSP,
  input  [7:0] SPIN,
  input  INIT,
  output [15:0] RAM_ADDR,
  output RAM_WE,
  output [15:0] RAM_VAL,
  output [15:0] POP_VAL,
  output [15:0] SPOUT
);

  wire controlled_buffer_1_out, controlled_buffer_4_out, del_not16_1_q, del_not16_2_q, nor_1_out,
       pull_resistor_1_node, xor_1_out;
  wire [7:0] controlled_buffer_2_out;

  assign controlled_buffer_1_out = LDSP ? LDSP : 1'bz;  // Controlled_Buffer controlled_buffer_1
  assign controlled_buffer_2_out = LDSP ? SPIN : 8'bz;  // Controlled_Buffer controlled_buffer_2
  DEL_NOT16 del_not16_1 (.D(POP), .Q(del_not16_1_q));
  DEL_NOT16 del_not16_2 (.D(del_not16_1_q), .Q(del_not16_2_q));
  assign controlled_buffer_1_out = INIT ? INIT : 1'bz;  // Controlled_Buffer controlled_buffer_3
  nor nor_1 (nor_1_out, ~PUSH, del_not16_2_q);  // NOR_Gate
  assign controlled_buffer_4_out = nor_1_out ? nor_1_out : 1'bz;  // Controlled_Buffer controlled_buffer_4
  Pull_Resistor pull_resistor_1 (.node(pull_resistor_1_node));
  xor xor_1 (xor_1_out, del_not16_2_q, PUSH);
  assign pull_resistor_1_node = xor_1_out ? xor_1_out : 1'bz;  // Controlled_Buffer controlled_buffer_5
  Pull_Resistor pull_resistor_2 ();  // open: node
  Pull_Resistor pull_resistor_3 (.node(controlled_buffer_1_out));
  assign controlled_buffer_2_out = INIT ? {8{1'b0}} : 8'bz;  // Controlled_Buffer controlled_buffer_6
  Counter #(.max('hfefe), .width(16)) counter_1 (
    .load(controlled_buffer_1_out), .up(controlled_buffer_4_out), .clk(pull_resistor_1_node),
    .D({8'hfe, controlled_buffer_2_out}), .Q(RAM_ADDR));  // open: clr, count, carry
  Pull_Resistor pull_resistor_4 (.node(controlled_buffer_4_out));
  assign controlled_buffer_4_out = controlled_buffer_1_out ? controlled_buffer_1_out : 1'bz;  // Controlled_Buffer controlled_buffer_7
  assign pull_resistor_1_node = controlled_buffer_1_out ? controlled_buffer_1_out : 1'bz;  // Controlled_Buffer controlled_buffer_8

  assign RAM_VAL = PUSH_VAL;
  assign RAM_WE = PUSH;
  assign SPOUT = RAM_ADDR;

  // Notes on the sheet:
  //   TOP
endmodule

module LowClock (
  output CLKSIG
);

  wire clock_1_out, not_1_out;

  Clock clock_1 (.out(clock_1_out));
  not not_1 (not_1_out, clock_1_out);
  and and_1 (CLKSIG, clock_1_out, not_1_out);
endmodule

module RegColCtrl (
  input  RSA,
  input  RSB,
  input  RSC,
  input  RSD,
  input  WSA,
  input  WSB,
  input  WSC,
  input  WSD,
  output REG_ENBL,
  output [2:0] RSEL,
  output [2:0] WSEL
);

  wire xor_2_out, xor_3_out;

  assign RSEL = RSA ? 3'b000 : 3'bz;  // Controlled_Buffer controlled_buffer_1
  assign RSEL = RSB ? 3'b001 : 3'bz;  // Controlled_Buffer controlled_buffer_2
  xor xor_1 (REG_ENBL, xor_2_out, xor_3_out);
  ExactlyOne xor_2 (.out(xor_2_out), .in0(RSD), .in1(RSC), .in2(RSB), .in3(RSA));
  ExactlyOne xor_3 (.out(xor_3_out), .in0(WSA), .in1(WSB), .in2(WSC), .in3(WSD));
  assign RSEL = RSC ? 3'b010 : 3'bz;  // Controlled_Buffer controlled_buffer_3
  assign WSEL = WSB ? 3'b010 : 3'bz;  // Controlled_Buffer controlled_buffer_4
  assign RSEL = RSD ? 3'b011 : 3'bz;  // Controlled_Buffer controlled_buffer_5
  assign WSEL = WSA ? 3'b011 : 3'bz;  // Controlled_Buffer controlled_buffer_6
  assign WSEL = WSD ? 3'b000 : 3'bz;  // Controlled_Buffer controlled_buffer_7
  assign WSEL = WSC ? 3'b001 : 3'bz;  // Controlled_Buffer controlled_buffer_8

  // Other names for the same wires on the sheet: WSA_t = WSD; WSB_t = WSC; WSC_t = WSB; WSD_t = WSA
endmodule
