// Logisim project AFlix_Backup_Jump_Circuitry.circ as structural Verilog: 18 circuits, main circuit sketch
module FULLADDER (
  input  Ci,
  input  A,
  input  B,
  output S,
  output Co
);

  wire and_1_out, and_2_out, xor_1_out;

  xor xor_1 (xor_1_out, A, B);
  and and_1 (and_1_out, A, B);
  xor xor_2 (S, xor_1_out, Ci);
  and and_2 (and_2_out, xor_1_out, Ci);
  or or_1 (Co, and_2_out, and_1_out);
endmodule

module ALU1 (
  input  A,
  input  B,
  input  AINV,
  input  BINV,
  input  Ci,
  input  OP_XOR,
  input  OP_SUM,
  input  OP_OR,
  input  OP_AND,
  output Co,
  output R
);

  wire and_1_out, fulladder_1_s, or_1_out, xor_1_out, xor_2_out, xor_3_out;

  xor xor_1 (xor_1_out, A, AINV);
  FULLADDER fulladder_1 (.Ci(Ci), .A(xor_1_out), .B(xor_2_out), .S(fulladder_1_s), .Co(Co));
  assign R = OP_SUM ? fulladder_1_s : 1'bz;  // Controlled_Buffer controlled_buffer_1
  or or_1 (or_1_out, xor_1_out, xor_2_out);
  assign R = OP_OR ? or_1_out : 1'bz;  // Controlled_Buffer controlled_buffer_2
  Pull_Resistor pull_resistor_1 (.node(R));
  and and_1 (and_1_out, xor_1_out, xor_2_out);
  assign R = OP_AND ? and_1_out : 1'bz;  // Controlled_Buffer controlled_buffer_3
  xor xor_2 (xor_2_out, B, BINV);
  assign R = OP_XOR ? xor_3_out : 1'bz;  // Controlled_Buffer controlled_buffer_4
  xor xor_3 (xor_3_out, xor_2_out, xor_1_out);
endmodule

module ALU16 (
  input  OP_AINV,
  input  OP_BINV,
  input  OP_SUM,
  input  OP_OR,
  input  OP_AND,
  input  Ci,
  input  OP_XOR,
  input  [15:0] A,
  input  [15:0] B,
  output [15:0] R,
  output [3:0] FLAGS,
  output FLAGS_WE
);

  wire alu1_1_co, alu1_2_co, alu1_3_co, alu1_4_co, alu1_5_co, alu1_6_co, alu1_7_co, alu1_8_co, alu1_9_co,
       alu1_10_co, alu1_11_co, alu1_12_co, alu1_13_co, alu1_14_co, alu1_15_co, alu1_16_co,
       controlled_buffer_5_out, nor_1_out, or_1_out, xor_1_out;
  wire [15:0] AT, BT;

  Pull_Resistor pull_resistor_1 (.node(FLAGS[0]));
  Pull_Resistor pull_resistor_2 (.node(FLAGS[1]));
  Pull_Resistor pull_resistor_3 (.node(FLAGS[2]));
  Pull_Resistor pull_resistor_4 (.node(FLAGS[3]));
  assign FLAGS[0] = OP_SUM ? alu1_1_co : 1'bz;  // Controlled_Buffer controlled_buffer_1
  assign FLAGS[1] = OP_SUM ? xor_1_out : 1'bz;  // Controlled_Buffer controlled_buffer_2
  assign FLAGS[2] = OP_SUM ? R[15] : 1'bz;  // Controlled_Buffer controlled_buffer_3
  assign FLAGS[3] = OP_SUM ? controlled_buffer_5_out : 1'bz;  // Controlled_Buffer controlled_buffer_4
  xor xor_1 (xor_1_out, alu1_1_co, alu1_2_co);
  assign controlled_buffer_5_out = OP_SUM ? nor_1_out : 1'bz;  // Controlled_Buffer controlled_buffer_5
  nor nor_1 (nor_1_out, R[0], R[1], R[2], R[3], R[4], R[5], R[6], R[7], R[8], R[9], R[10], R[11], R[12], R[13], R[14], R[15]);
  assign AT = or_1_out ? A : 16'bz;  // Controlled_Buffer controlled_buffer_6
  assign BT = or_1_out ? B : 16'bz;  // Controlled_Buffer controlled_buffer_7
  or or_1 (or_1_out, OP_AND, OP_OR, OP_SUM, OP_BINV, OP_AINV);
  ALU1 alu1_1 (
    .A(AT[15]), .B(BT[15]), .AINV(OP_AINV), .BINV(OP_BINV), .Ci(alu1_2_co), .OP_XOR(OP_XOR), .OP_SUM(OP_SUM),
    .OP_OR(OP_OR), .OP_AND(OP_AND), .Co(alu1_1_co), .R(R[15]));
  ALU1 alu1_2 (
    .A(AT[14]), .B(BT[14]), .AINV(OP_AINV), .BINV(OP_BINV), .Ci(alu1_3_co), .OP_XOR(OP_XOR), .OP_SUM(OP_SUM),
    .OP_OR(OP_OR), .OP_AND(OP_AND), .Co(alu1_2_co), .R(R[14]));
  ALU1 alu1_3 (
    .A(AT[13]), .B(BT[13]), .AINV(OP_AINV), .BINV(OP_BINV), .Ci(alu1_4_co), .OP_XOR(OP_XOR), .OP_SUM(OP_SUM),
    .OP_OR(OP_OR), .OP_AND(OP_AND), .Co(alu1_3_co), .R(R[13]));
  ALU1 alu1_4 (
    .A(AT[12]), .B(BT[12]), .AINV(OP_AINV), .BINV(OP_BINV), .Ci(alu1_5_co), .OP_XOR(OP_XOR), .OP_SUM(OP_SUM),
    .OP_OR(OP_OR), .OP_AND(OP_AND), .Co(alu1_4_co), .R(R[12]));
  ALU1 alu1_5 (
    .A(AT[11]), .B(BT[11]), .AINV(OP_AINV), .BINV(OP_BINV), .Ci(alu1_6_co), .OP_XOR(OP_XOR), .OP_SUM(OP_SUM),
    .OP_OR(OP_OR), .OP_AND(OP_AND), .Co(alu1_5_co), .R(R[11]));
  ALU1 alu1_6 (
    .A(AT[10]), .B(BT[10]), .AINV(OP_AINV), .BINV(OP_BINV), .Ci(alu1_7_co), .OP_XOR(OP_XOR), .OP_SUM(OP_SUM),
    .OP_OR(OP_OR), .OP_AND(OP_AND), .Co(alu1_6_co), .R(R[10]));
  ALU1 alu1_7 (
    .A(AT[9]), .B(BT[9]), .AINV(OP_AINV), .BINV(OP_BINV), .Ci(alu1_8_co), .OP_XOR(OP_XOR), .OP_SUM(OP_SUM),
    .OP_OR(OP_OR), .OP_AND(OP_AND), .Co(alu1_7_co), .R(R[9]));
  ALU1 alu1_8 (
    .A(AT[8]), .B(BT[8]), .AINV(OP_AINV), .BINV(OP_BINV), .Ci(alu1_9_co), .OP_XOR(OP_XOR), .OP_SUM(OP_SUM),
    .OP_OR(OP_OR), .OP_AND(OP_AND), .Co(alu1_8_co), .R(R[8]));
  ALU1 alu1_9 (
    .A(AT[7]), .B(BT[7]), .AINV(OP_AINV), .BINV(OP_BINV), .Ci(alu1_10_co), .OP_XOR(OP_XOR), .OP_SUM(OP_SUM),
    .OP_OR(OP_OR), .OP_AND(OP_AND), .Co(alu1_9_co), .R(R[7]));
  ALU1 alu1_10 (
    .A(AT[6]), .B(BT[6]), .AINV(OP_AINV), .BINV(OP_BINV), .Ci(alu1_11_co), .OP_XOR(OP_XOR), .OP_SUM(OP_SUM),
    .OP_OR(OP_OR), .OP_AND(OP_AND), .Co(alu1_10_co), .R(R[6]));
  ALU1 alu1_11 (
    .A(AT[5]), .B(BT[5]), .AINV(OP_AINV), .BINV(OP_BINV), .Ci(alu1_12_co), .OP_XOR(OP_XOR), .OP_SUM(OP_SUM),
    .OP_OR(OP_OR), .OP_AND(OP_AND), .Co(alu1_11_co), .R(R[5]));
  ALU1 alu1_12 (
    .A(AT[4]), .B(BT[4]), .AINV(OP_AINV), .BINV(OP_BINV), .Ci(alu1_13_co), .OP_XOR(OP_XOR), .OP_SUM(OP_SUM),
    .OP_OR(OP_OR), .OP_AND(OP_AND), .Co(alu1_12_co), .R(R[4]));
  ALU1 alu1_13 (
    .A(AT[3]), .B(BT[3]), .AINV(OP_AINV), .BINV(OP_BINV), .Ci(alu1_14_co), .OP_XOR(OP_XOR), .OP_SUM(OP_SUM),
    .OP_OR(OP_OR), .OP_AND(OP_AND), .Co(alu1_13_co), .R(R[3]));
  ALU1 alu1_14 (
    .A(AT[2]), .B(BT[2]), .AINV(OP_AINV), .BINV(OP_BINV), .Ci(alu1_15_co), .OP_XOR(OP_XOR), .OP_SUM(OP_SUM),
    .OP_OR(OP_OR), .OP_AND(OP_AND), .Co(alu1_14_co), .R(R[2]));
  ALU1 alu1_15 (
    .A(AT[1]), .B(BT[1]), .AINV(OP_AINV), .BINV(OP_BINV), .Ci(alu1_16_co), .OP_XOR(OP_XOR), .OP_SUM(OP_SUM),
    .OP_OR(OP_OR), .OP_AND(OP_AND), .Co(alu1_15_co), .R(R[1]));
  ALU1 alu1_16 (
    .A(AT[0]), .B(BT[0]), .AINV(OP_AINV), .BINV(OP_BINV), .Ci(Ci), .OP_XOR(OP_XOR), .OP_SUM(OP_SUM),
    .OP_OR(OP_OR), .OP_AND(OP_AND), .Co(alu1_16_co), .R(R[0]));

  assign FLAGS_WE = OP_SUM;

  // Other names for the same wires on the sheet: AIT = OP_AINV; ANT = OP_AND; BIT = OP_BINV; CiT = Ci; ORT = OP_OR;
  //   RT[15:0] = R; SUT = OP_SUM; XOT = OP_XOR
endmodule

module DEL_NOT16 (
  input  D,
  output Q
);

  wire not_1_out, not_2_out, not_3_out, not_4_out, not_5_out, not_6_out, not_8_out, not_9_out, not_10_out,
       not_11_out, not_12_out, not_13_out, not_14_out, not_15_out, not_16_out, not_17_out, not_18_out,
       not_19_out, not_20_out, not_21_out, not_22_out, not_23_out, not_24_out;

  not not_1 (not_1_out, not_4_out);
  not not_2 (not_2_out, not_5_out);
  not not_3 (not_3_out, not_6_out);
  not not_4 (not_4_out, not_2_out);
  not not_5 (not_5_out, not_3_out);
  not not_6 (not_6_out, not_13_out);
  not not_7 (Q, not_10_out);
  not not_8 (not_8_out, not_11_out);
  not not_9 (not_9_out, not_12_out);
  not not_10 (not_10_out, not_8_out);
  not not_11 (not_11_out, not_9_out);
  not not_12 (not_12_out, not_19_out);
  not not_13 (not_13_out, not_16_out);
  not not_14 (not_14_out, not_17_out);
  not not_15 (not_15_out, not_18_out);
  not not_16 (not_16_out, not_14_out);
  not not_17 (not_17_out, not_15_out);
  not not_18 (not_18_out, D);
  not not_19 (not_19_out, not_22_out);
  not not_20 (not_20_out, not_23_out);
  not not_21 (not_21_out, not_24_out);
  not not_22 (not_22_out, not_20_out);
  not not_23 (not_23_out, not_21_out);
  not not_24 (not_24_out, not_1_out);
endmodule

module sketch (
  input  Exec,
  input  CONTINUE
);

  wire ACC_WR, alu16_1_flags_we, alu16ctrl_1_q_ainv, alu16ctrl_1_q_and, alu16ctrl_1_q_binv, alu16ctrl_1_q_ci,
       alu16ctrl_1_q_or, alu16ctrl_1_q_sum, alu16ctrl_1_q_xor, ALU_ENB, and_1_out, and_3_out, and_4_out,
       and_5_out, and_6_out, CLK, CLK_clksig, decoder_1_out0, decoder_1_out1, decoder_1_out2, decoder_1_out3,
       decoder_1_out4, decoder_1_out5, decoder_2_out0, decoder_2_out1, decoder_2_out2, decoder_2_out3,
       decoder_2_out4, decoder_2_out5, del_not16_2_q, del_not16_3_q, DESP, DIN_ENB, HALT, JMP, JRA, LDSP,
       not_1_out, not_2_out, not_3_out, not_4_out, or_1_out, PHI, PHR, PLR, pull_resistor_3_node,
       RAM_ADDRIN_ENBL, RDSP, ReadFromReg, REG_ENABLE, RFI, RIP, RSA, RSB, RSC, RSD, RSH, RSL, RSRA, RSX,
       SRST, STACK_CTRL_p9, STACK_INSTR, WIP, WSA, WSB, WSC, WSD, WSH, WSL, WSRA, WSX, xor_1_out, xor_2_out,
       xor_3_out, xor_4_out, xor_5_out, xor_6_out, xor_7_out, xor_8_out, xor_9_out, xor_10_out, xor_11_out,
       xor_12_out, xor_13_out, xor_14_out, xor_15_out, xor_16_out, xor_17_out, xor_18_out, xor_19_out,
       xor_20_out, xor_21_out, xor_23_out, xor_24_out, xor_25_out, xor_26_out, xor_27_out, xor_28_out,
       xor_29_out, xor_30_out, xor_31_out, xor_32_out, xor_33_out, XOR_RAM_STACK_REQ_out, ZF;
  wire [2:0] bit_extender_1_out, bit_extender_4_out, GPREG_CTRL_rsel, GPREG_CTRL_wsel, register_1_q;
  wire [3:0] alu16_1_flags;
  wire [7:0] controlled_buffer_34_out, HI8, LO8;
  wire [15:0] ACC_OUT, alu16_1_r, controlled_buffer_33_out, controlled_buffer_35_out, GPREGS_dout,
       GPREGS_rra_out, groupinglogic_1_x, HI16, IPT, JMP_DEST, LO16, PushVal, ram_1_dout, RAM_Addr,
       RAM_ALU_OUT, RegCol_DIN, STACK_CTRL_p8, STACK_CTRL_p10, STACK_CTRL_p11, X16;
  wire [23:0] rom_1_data;
  wire [31:0] groupinglogic_1_alu, groupinglogic_1_iload, groupinglogic_1_misc, groupinglogic_1_reserved1,
       groupinglogic_1_reserved2, groupinglogic_1_rload, groupinglogic_1_stack, groupinglogic_1_store;

  LED led_1 (.in(rom_1_data[0]));
  LED led_2 (.in(rom_1_data[1]));
  LED led_3 (.in(rom_1_data[2]));
  LED led_4 (.in(rom_1_data[3]));
  LED led_5 (.in(rom_1_data[4]));
  LED led_6 (.in(rom_1_data[5]));
  LED led_7 (.in(rom_1_data[6]));
  LED led_8 (.in(rom_1_data[7]));
  LED led_9 (.in(rom_1_data[8]));
  LED led_10 (.in(rom_1_data[9]));
  LED led_11 (.in(rom_1_data[10]));
  LED led_12 (.in(rom_1_data[11]));
  LED led_13 (.in(rom_1_data[12]));
  LED led_14 (.in(rom_1_data[13]));
  LED led_15 (.in(rom_1_data[14]));
  LED led_16 (.in(rom_1_data[15]));
  LED led_17 (.in(rom_1_data[16]));
  LED led_18 (.in(rom_1_data[17]));
  LED led_19 (.in(rom_1_data[18]));
  LED led_20 (.in(rom_1_data[19]));
  LED led_21 (.in(rom_1_data[20]));
  LED led_22 (.in(rom_1_data[21]));
  LED led_23 (.in(rom_1_data[22]));
  LED led_24 (.in(rom_1_data[23]));
  // Digital_Oscilloscope #(.frontlines("both"), .nState(8)) Oszi: pin names not known; wires that end beside it: CLK
  xor xor_1 (xor_1_out, HALT, CONTINUE);
  LowClock u_CLK (.CLKSIG(CLK_clksig));
  and and_1 (and_1_out, CLK_clksig, Exec);
  and and_2 (CLK, ~xor_1_out, and_1_out);  // AND_Gate
  Pull_Resistor pull_resistor_1 (.node(JMP));
  IP IPREG (.JMP(JMP), .CLK(CLK), .JMPLOC(JMP_DEST), .IPOUT(IPT));
  ROM #(.addrWidth(16), .dataWidth(24)) rom_1 (.addr(IPT), .data(rom_1_data));
  assign WSX = PLR ? PLR : 1'bz;  // Controlled_Buffer controlled_buffer_1
  assign WSA = PLR ? decoder_1_out0 : 1'bz;  // Controlled_Buffer controlled_buffer_2
  assign WSB = PLR ? decoder_1_out1 : 1'bz;  // Controlled_Buffer controlled_buffer_3
  Pull_Resistor pull_resistor_2 (.node(WIP));
  GroupingLogic groupinglogic_1 (
    .Execute(Exec), .Instruction(rom_1_data), .ILOAD(groupinglogic_1_iload), .RLOAD(groupinglogic_1_rload),
    .STORE(groupinglogic_1_store), .ALU(groupinglogic_1_alu), .HI(LO8), .LO(HI8), .X(groupinglogic_1_x),
    .STACK(groupinglogic_1_stack),
    .MISC({groupinglogic_1_misc[31], HALT, groupinglogic_1_misc[29:27], JRA, groupinglogic_1_misc[25:0]}),
    .RESERVED1(groupinglogic_1_reserved1), .RESERVED2(groupinglogic_1_reserved2));
  Bit_Extender #(.out_width(3), .\type ("zero")) bit_extender_1 (.in(HI8), .out(bit_extender_1_out));
  Decoder #(.enable("false"), .select(3)) decoder_1 (
    .out0(decoder_1_out0), .out1(decoder_1_out1), .out2(decoder_1_out2), .out3(decoder_1_out3),
    .out4(decoder_1_out4), .out5(decoder_1_out5), .sel(bit_extender_1_out));  // open: out6, out7
  assign WSC = PLR ? decoder_1_out2 : 1'bz;  // Controlled_Buffer controlled_buffer_4
  assign WSD = PLR ? decoder_1_out3 : 1'bz;  // Controlled_Buffer controlled_buffer_5
  assign WSRA = PLR ? decoder_1_out4 : 1'bz;  // Controlled_Buffer controlled_buffer_6
  assign WIP = PLR ? decoder_1_out5 : 1'bz;  // Controlled_Buffer controlled_buffer_7
  assign JMP = JRA ? JRA : 1'bz;  // Controlled_Buffer controlled_buffer_8
  // Probe on GPREGS_rra_out
  assign JMP = pull_resistor_3_node ? pull_resistor_3_node : 1'bz;  // Controlled_Buffer controlled_buffer_9
  Pull_Resistor pull_resistor_3 (.node(pull_resistor_3_node));
  assign pull_resistor_3_node = WIP ? WIP : 1'bz;  // Controlled_Buffer controlled_buffer_10
  Pull_Resistor pull_resistor_4 (.node(WSRA));
  assign WSRA = xor_2_out ? xor_2_out : 1'bz;  // Controlled_Buffer controlled_buffer_11
  ExactlyOne xor_2 (
    .out(xor_2_out), .in0(groupinglogic_1_iload[14]), .in1(groupinglogic_1_iload[13]),
    .in2(groupinglogic_1_iload[12]));
  assign HI16 = {{8{1'b0}}, HI8};  // Bit_Extender bit_extender_2
  assign LO16 = {{8{1'b0}}, LO8};  // Bit_Extender bit_extender_3
  assign RAM_Addr = RAM_ADDRIN_ENBL ? groupinglogic_1_x : 16'bz;  // Controlled_Buffer controlled_buffer_12
  assign X16 = not_1_out ? groupinglogic_1_x : 16'bz;  // Controlled_Buffer controlled_buffer_13
  assign X16 = RIP ? IPT : 16'bz;  // Controlled_Buffer controlled_buffer_14
  not not_1 (not_1_out, RIP);
  assign RSX = PHR ? PHR : 1'bz;  // Controlled_Buffer controlled_buffer_15
  // Probe on RegCol_DIN
  Pull_Resistor pull_resistor_5 (.node(RegCol_DIN));
  assign JMP_DEST = pull_resistor_3_node ? RegCol_DIN : 16'bz;  // Controlled_Buffer controlled_buffer_16
  assign JMP_DEST = JRA ? GPREGS_rra_out : 16'bz;  // Controlled_Buffer controlled_buffer_17
  Pull_Resistor pull_resistor_6 (.node(WSD));
  Pull_Resistor pull_resistor_7 (.node(WSC));
  Pull_Resistor pull_resistor_8 (.node(WSB));
  assign WSD = xor_3_out ? xor_3_out : 1'bz;  // Controlled_Buffer controlled_buffer_18
  assign WSC = xor_4_out ? xor_4_out : 1'bz;  // Controlled_Buffer controlled_buffer_19
  assign WSB = xor_5_out ? xor_5_out : 1'bz;  // Controlled_Buffer controlled_buffer_20
  ExactlyOne xor_3 (
    .out(xor_3_out), .in0(groupinglogic_1_iload[11]), .in1(groupinglogic_1_iload[10]),
    .in2(groupinglogic_1_iload[9]));
  ExactlyOne xor_4 (
    .out(xor_4_out), .in0(groupinglogic_1_iload[8]), .in1(groupinglogic_1_iload[7]),
    .in2(groupinglogic_1_iload[6]));
  ExactlyOne xor_5 (
    .out(xor_5_out), .in0(groupinglogic_1_iload[5]), .in1(groupinglogic_1_iload[4]),
    .in2(groupinglogic_1_iload[3]));
  not not_2 (not_2_out, DIN_ENB);
  ExactlyOne xor_6 (.out(xor_6_out), .in0(not_2_out), .in1(RDSP), .in2(PLR), .in3(ALU_ENB));
  assign RegCol_DIN = xor_6_out ? groupinglogic_1_x : 16'bz;  // Controlled_Buffer controlled_buffer_21
  assign RSA = PHR ? decoder_2_out0 : 1'bz;  // Controlled_Buffer controlled_buffer_22
  assign RSB = PHR ? decoder_2_out1 : 1'bz;  // Controlled_Buffer controlled_buffer_23
  assign RSC = PHR ? decoder_2_out2 : 1'bz;  // Controlled_Buffer controlled_buffer_24
  assign RSD = PHR ? decoder_2_out3 : 1'bz;  // Controlled_Buffer controlled_buffer_25
  assign RSRA = PHR ? decoder_2_out4 : 1'bz;  // Controlled_Buffer controlled_buffer_26
  Pull_Resistor pull_resistor_9 (.node(RIP));
  RegColCtrl GPREG_CTRL (
    .RSRA(RSRA), .WSRA(WSRA), .RSA(RSA), .WSA(WSA), .RSB(RSB), .WSB(WSB), .RSC(RSC), .WSC(WSC), .RSD(RSD),
    .WSD(WSD), .RSEL(GPREG_CTRL_rsel), .REG_ENBL(REG_ENABLE), .WSEL(GPREG_CTRL_wsel));
  RegCol GPREGS (
    .ENBL(REG_ENABLE), .RX(RSX), .RH(RSH), .RL(RSL), .WX(WSX), .WH(WSH), .WL(WSL), .CLK(CLK),
    .RSEL(GPREG_CTRL_rsel), .WSEL(GPREG_CTRL_wsel), .DIN(RegCol_DIN), .ACC_WR(ACC_WR),
    .RRA_OUT(GPREGS_rra_out), .ACC_OUT(ACC_OUT), .DOUT(GPREGS_dout));
  Pull_Resistor pull_resistor_10 (.node(WSX));
  assign WSX = xor_7_out ? xor_7_out : 1'bz;  // Controlled_Buffer controlled_buffer_27
  Pull_Resistor pull_resistor_11 (.node(WSA));
  assign WSA = xor_8_out ? xor_8_out : 1'bz;  // Controlled_Buffer controlled_buffer_28
  ExactlyOne xor_7 (
    .out(xor_7_out), .in0(groupinglogic_1_iload[9]), .in1(groupinglogic_1_iload[6]),
    .in2(groupinglogic_1_iload[12]), .in3(groupinglogic_1_iload[3]), .in4(groupinglogic_1_iload[0]));
  ExactlyOne xor_8 (
    .out(xor_8_out), .in0(groupinglogic_1_iload[2]), .in1(groupinglogic_1_iload[1]),
    .in2(groupinglogic_1_iload[0]));
  Pull_Resistor pull_resistor_12 (.node(RAM_ADDRIN_ENBL));
  Bit_Extender #(.out_width(3), .\type ("zero")) bit_extender_4 (.in(HI8), .out(bit_extender_4_out));
  Decoder #(.enable("false"), .select(3)) decoder_2 (
    .out0(decoder_2_out0), .out1(decoder_2_out1), .out2(decoder_2_out2), .out3(decoder_2_out3),
    .out4(decoder_2_out4), .out5(decoder_2_out5), .sel(bit_extender_4_out));  // open: out6, out7
  assign RIP = PHR ? decoder_2_out5 : 1'bz;  // Controlled_Buffer controlled_buffer_29
  ExactlyOne xor_9 (.out(xor_9_out), .in0(RSX), .in1(RSH), .in2(RSL));
  Pull_Resistor pull_resistor_13 (.node(WSH));
  assign WSH = xor_10_out ? xor_10_out : 1'bz;  // Controlled_Buffer controlled_buffer_30
  ExactlyOne xor_10 (
    .out(xor_10_out), .in0(groupinglogic_1_iload[10]), .in1(groupinglogic_1_iload[7]),
    .in2(groupinglogic_1_iload[13]), .in3(groupinglogic_1_iload[4]), .in4(groupinglogic_1_iload[1]));
  not not_3 (not_3_out, RIP);
  Pull_Resistor pull_resistor_14 (.node(ReadFromReg));
  assign ReadFromReg = not_3_out ? xor_9_out : 1'bz;  // Controlled_Buffer controlled_buffer_31
  Pull_Resistor pull_resistor_15 (.node(WSL));
  assign WSL = xor_11_out ? xor_11_out : 1'bz;  // Controlled_Buffer controlled_buffer_32
  ExactlyOne xor_11 (
    .out(xor_11_out), .in0(groupinglogic_1_iload[11]), .in1(groupinglogic_1_iload[8]),
    .in2(groupinglogic_1_iload[14]), .in3(groupinglogic_1_iload[5]), .in4(groupinglogic_1_iload[2]));
  // Probe on GPREGS_dout
  Pull_Resistor pull_resistor_16 (.node(GPREGS_dout));
  assign controlled_buffer_33_out = xor_12_out ? X16 : 16'bz;  // Controlled_Buffer controlled_buffer_33
  assign controlled_buffer_34_out = LDSP ? LO8 : 8'bz;  // Controlled_Buffer controlled_buffer_34
  assign controlled_buffer_35_out = RAM_ADDRIN_ENBL ? RAM_Addr : 16'bz;  // Controlled_Buffer controlled_buffer_35
  xor xor_12 (xor_12_out, PHR, PHI);
  // Stack256 STACK_CTRL: pin names not known; wires that end beside it: xor_12_out, controlled_buffer_33_out, DESP, SRST, controlled_buffer_34_out, CLK, LDSP, STACK_CTRL_p8, STACK_CTRL_p9, STACK_CTRL_p10, STACK_CTRL_p11
  assign controlled_buffer_35_out = STACK_INSTR ? STACK_CTRL_p8 : 16'bz;  // Controlled_Buffer controlled_buffer_36
  RAM #(.addrWidth(16), .dataWidth(16), .enables("line")) ram_1 (
    .addr(controlled_buffer_35_out), .we(or_1_out), .clk(CLK), .din(PushVal), .dout(ram_1_dout));
  or or_1 (or_1_out, STACK_CTRL_p9, ReadFromReg);
  assign PushVal = ReadFromReg ? GPREGS_dout : 16'bz;  // Controlled_Buffer controlled_buffer_37
  xor xor_13 (xor_13_out, PHI, RIP);
  assign PushVal = xor_13_out ? STACK_CTRL_p10 : 16'bz;  // Controlled_Buffer controlled_buffer_38
  Pull_Resistor pull_resistor_17 (.node(WSRA));
  assign WSRA = xor_14_out ? xor_14_out : 1'bz;  // Controlled_Buffer controlled_buffer_39
  ExactlyOne xor_14 (
    .out(xor_14_out), .in0(groupinglogic_1_rload[14]), .in1(groupinglogic_1_rload[13]),
    .in2(groupinglogic_1_rload[12]));
  Pull_Resistor pull_resistor_18 (.node(WSD));
  Pull_Resistor pull_resistor_19 (.node(WSC));
  Pull_Resistor pull_resistor_20 (.node(WSB));
  assign WSD = xor_15_out ? xor_15_out : 1'bz;  // Controlled_Buffer controlled_buffer_40
  assign WSC = xor_16_out ? xor_16_out : 1'bz;  // Controlled_Buffer controlled_buffer_41
  assign WSB = xor_17_out ? xor_17_out : 1'bz;  // Controlled_Buffer controlled_buffer_42
  ExactlyOne xor_15 (
    .out(xor_15_out), .in0(groupinglogic_1_rload[11]), .in1(groupinglogic_1_rload[10]),
    .in2(groupinglogic_1_rload[9]));
  ExactlyOne xor_16 (
    .out(xor_16_out), .in0(groupinglogic_1_rload[8]), .in1(groupinglogic_1_rload[7]),
    .in2(groupinglogic_1_rload[6]));
  ExactlyOne xor_17 (
    .out(xor_17_out), .in0(groupinglogic_1_rload[5]), .in1(groupinglogic_1_rload[4]),
    .in2(groupinglogic_1_rload[3]));
  Pull_Resistor pull_resistor_21 (.node(ram_1_dout));
  Pull_Resistor pull_resistor_22 (.node(WSA));
  Pull_Resistor pull_resistor_23 (.node(WSX));
  assign WSA = xor_18_out ? xor_18_out : 1'bz;  // Controlled_Buffer controlled_buffer_43
  assign WSX = xor_19_out ? xor_19_out : 1'bz;  // Controlled_Buffer controlled_buffer_44
  ExactlyOne xor_18 (
    .out(xor_18_out), .in0(groupinglogic_1_rload[2]), .in1(groupinglogic_1_rload[1]),
    .in2(groupinglogic_1_rload[0]));
  ExactlyOne xor_19 (
    .out(xor_19_out), .in0(groupinglogic_1_rload[9]), .in1(groupinglogic_1_rload[6]),
    .in2(groupinglogic_1_rload[12]), .in3(groupinglogic_1_rload[3]), .in4(groupinglogic_1_rload[0]));
  assign RegCol_DIN = RDSP ? STACK_CTRL_p11 : 16'bz;  // Controlled_Buffer controlled_buffer_45
  Pull_Resistor pull_resistor_24 (.node(WSH));
  assign WSH = xor_20_out ? xor_20_out : 1'bz;  // Controlled_Buffer controlled_buffer_46
  ExactlyOne xor_20 (
    .out(xor_20_out), .in0(groupinglogic_1_rload[10]), .in1(groupinglogic_1_rload[7]),
    .in2(groupinglogic_1_rload[13]), .in3(groupinglogic_1_rload[4]), .in4(groupinglogic_1_rload[1]));
  xor xor_21 (xor_21_out, PLR, DIN_ENB);
  assign RAM_ALU_OUT = and_3_out ? ram_1_dout : 16'bz;  // Controlled_Buffer controlled_buffer_47
  assign RAM_ALU_OUT = not_4_out ? 16'h1 : 16'bz;  // Controlled_Buffer controlled_buffer_48
  not not_4 (not_4_out, and_3_out);
  assign RAM_ADDRIN_ENBL = DIN_ENB ? DIN_ENB : 1'bz;  // Controlled_Buffer controlled_buffer_49
  ExactlyOne xor_22 (.out(DIN_ENB), .in0(xor_19_out), .in1(xor_20_out), .in2(xor_23_out));
  Pull_Resistor pull_resistor_25 (.node(WSL));
  assign WSL = xor_23_out ? xor_23_out : 1'bz;  // Controlled_Buffer controlled_buffer_50
  ExactlyOne xor_23 (
    .out(xor_23_out), .in0(groupinglogic_1_rload[11]), .in1(groupinglogic_1_rload[8]),
    .in2(groupinglogic_1_rload[14]), .in3(groupinglogic_1_rload[5]), .in4(groupinglogic_1_rload[2]));
  assign RegCol_DIN = xor_21_out ? ram_1_dout : 16'bz;  // Controlled_Buffer controlled_buffer_51
  and and_3 (and_3_out, ALU_ENB, RAM_ADDRIN_ENBL);
  Pull_Resistor pull_resistor_26 (.node(RSRA));
  assign RSRA = xor_24_out ? xor_24_out : 1'bz;  // Controlled_Buffer controlled_buffer_52
  ExactlyOne xor_24 (
    .out(xor_24_out), .in0(groupinglogic_1_store[14]), .in1(groupinglogic_1_store[13]),
    .in2(groupinglogic_1_store[12]));
  Pull_Resistor pull_resistor_27 (.node(RSD));
  Pull_Resistor pull_resistor_28 (.node(RSC));
  Pull_Resistor pull_resistor_29 (.node(RSB));
  assign RSD = xor_25_out ? xor_25_out : 1'bz;  // Controlled_Buffer controlled_buffer_53
  assign RSC = xor_26_out ? xor_26_out : 1'bz;  // Controlled_Buffer controlled_buffer_54
  assign RSB = xor_27_out ? xor_27_out : 1'bz;  // Controlled_Buffer controlled_buffer_55
  ExactlyOne xor_25 (
    .out(xor_25_out), .in0(groupinglogic_1_store[11]), .in1(groupinglogic_1_store[10]),
    .in2(groupinglogic_1_store[9]));
  ExactlyOne xor_26 (
    .out(xor_26_out), .in0(groupinglogic_1_store[8]), .in1(groupinglogic_1_store[7]),
    .in2(groupinglogic_1_store[6]));
  ExactlyOne xor_27 (
    .out(xor_27_out), .in0(groupinglogic_1_store[5]), .in1(groupinglogic_1_store[4]),
    .in2(groupinglogic_1_store[3]));
  Register #(.width(4)) register_1 (
    .D(alu16_1_flags), .en(alu16_1_flags_we), .clk(CLK), .Q({ZF, register_1_q}));  // open: clr
  Pull_Resistor pull_resistor_30 (.node(RSX));
  assign RSX = xor_28_out ? xor_28_out : 1'bz;  // Controlled_Buffer controlled_buffer_56
  Pull_Resistor pull_resistor_31 (.node(RSA));
  assign RSA = xor_29_out ? xor_29_out : 1'bz;  // Controlled_Buffer controlled_buffer_57
  ExactlyOne xor_28 (
    .out(xor_28_out), .in0(groupinglogic_1_store[9]), .in1(groupinglogic_1_store[6]),
    .in2(groupinglogic_1_store[12]), .in3(groupinglogic_1_store[3]), .in4(groupinglogic_1_store[0]));
  ExactlyOne xor_29 (
    .out(xor_29_out), .in0(groupinglogic_1_store[2]), .in1(groupinglogic_1_store[1]),
    .in2(groupinglogic_1_store[0]));
  ExactlyOne xor_30 (.out(xor_30_out), .in0(xor_28_out), .in1(xor_31_out), .in2(xor_32_out));
  Pull_Resistor pull_resistor_32 (.node(RSH));
  assign RSH = xor_31_out ? xor_31_out : 1'bz;  // Controlled_Buffer controlled_buffer_58
  ExactlyOne xor_31 (
    .out(xor_31_out), .in0(groupinglogic_1_store[10]), .in1(groupinglogic_1_store[7]),
    .in2(groupinglogic_1_store[13]), .in3(groupinglogic_1_store[4]), .in4(groupinglogic_1_store[1]));
  LED Zero (.in(ZF));
  LED VFlow (.in(register_1_q[2]));
  LED Negative (.in(register_1_q[1]));
  LED CarryOut (.in(register_1_q[0]));
  ALU16 alu16_1 (
    .A(ACC_OUT), .B(RAM_ALU_OUT), .OP_AINV(alu16ctrl_1_q_ainv), .OP_BINV(alu16ctrl_1_q_binv),
    .OP_SUM(alu16ctrl_1_q_sum), .OP_OR(alu16ctrl_1_q_xor), .OP_AND(alu16ctrl_1_q_and), .Ci(alu16ctrl_1_q_ci),
    .OP_XOR(alu16ctrl_1_q_or), .R(alu16_1_r), .FLAGS(alu16_1_flags), .FLAGS_WE(alu16_1_flags_we));
  assign RegCol_DIN = ALU_ENB ? alu16_1_r : 16'bz;  // Controlled_Buffer controlled_buffer_59
  assign RAM_ADDRIN_ENBL = xor_30_out ? xor_30_out : 1'bz;  // Controlled_Buffer controlled_buffer_60
  Pull_Resistor pull_resistor_33 (.node(RSL));
  assign RSL = xor_32_out ? xor_32_out : 1'bz;  // Controlled_Buffer controlled_buffer_61
  ExactlyOne xor_32 (
    .out(xor_32_out), .in0(groupinglogic_1_store[11]), .in1(groupinglogic_1_store[8]),
    .in2(groupinglogic_1_store[14]), .in3(groupinglogic_1_store[5]), .in4(groupinglogic_1_store[2]));
  DEL_NOT16 del_not16_1 (.D(del_not16_2_q), .Q(ACC_WR));
  DEL_NOT16 del_not16_2 (.D(del_not16_3_q), .Q(del_not16_2_q));
  DEL_NOT16 del_not16_3 (.D(ALU_ENB), .Q(del_not16_3_q));
  assign RAM_ADDRIN_ENBL = and_4_out ? and_4_out : 1'bz;  // Controlled_Buffer controlled_buffer_62
  and and_4 (and_4_out, ALU_ENB, ~xor_33_out);  // AND_Gate
  xor xor_33 (xor_33_out, groupinglogic_1_alu[9], groupinglogic_1_alu[8]);
  ALU16Ctrl alu16ctrl_1 (
    .ALU_INC(groupinglogic_1_alu[8]), .ALU_DEC(groupinglogic_1_alu[9]), .ADD_OP(groupinglogic_1_alu[0]),
    .SUB_OP(groupinglogic_1_alu[1]), .AND_OP(groupinglogic_1_alu[2]), .OR_OP(groupinglogic_1_alu[3]),
    .NOT_OP(groupinglogic_1_alu[4]), .NOR_OP(groupinglogic_1_alu[5]), .NAND_OP(groupinglogic_1_alu[6]),
    .XOR_OP(groupinglogic_1_alu[7]), .Q_ENBL(ALU_ENB), .Q_OR(alu16ctrl_1_q_or), .Q_Ci(alu16ctrl_1_q_ci),
    .Q_AINV(alu16ctrl_1_q_ainv), .Q_BINV(alu16ctrl_1_q_binv), .Q_SUM(alu16ctrl_1_q_sum),
    .Q_AND(alu16ctrl_1_q_and), .Q_XOR(alu16ctrl_1_q_xor));
  Pull_Resistor pull_resistor_34 (.node(STACK_INSTR));
  assign STACK_INSTR = XOR_RAM_STACK_REQ_out ? XOR_RAM_STACK_REQ_out : 1'bz;  // Controlled_Buffer controlled_buffer_63
  ExactlyOne XOR_RAM_STACK_REQ (
    .out(XOR_RAM_STACK_REQ_out), .in0(groupinglogic_1_stack[1]), .in1(groupinglogic_1_stack[2]),
    .in2(groupinglogic_1_stack[3]), .in3(groupinglogic_1_stack[4]), .in4(groupinglogic_1_stack[5]),
    .in5(groupinglogic_1_stack[6]));
  assign WIP = groupinglogic_1_misc[29] ? groupinglogic_1_misc[29] : 1'bz;  // Controlled_Buffer controlled_buffer_64
  and and_5 (and_5_out, ZF, groupinglogic_1_misc[28]);
  and and_6 (and_6_out, ~ZF, groupinglogic_1_misc[27]);  // AND_Gate
  assign WIP = and_5_out ? and_5_out : 1'bz;  // Controlled_Buffer controlled_buffer_65
  assign WIP = and_6_out ? and_6_out : 1'bz;  // Controlled_Buffer controlled_buffer_66
  Pull_Resistor pull_resistor_35 (.node(DESP));
  assign DESP = groupinglogic_1_stack[7] ? groupinglogic_1_stack[7] : 1'bz;  // Controlled_Buffer controlled_buffer_67
  Pull_Resistor pull_resistor_36 (.node(RDSP));
  assign RDSP = groupinglogic_1_stack[6] ? groupinglogic_1_stack[6] : 1'bz;  // Controlled_Buffer controlled_buffer_68
  Pull_Resistor pull_resistor_37 (.node(LDSP));
  assign LDSP = groupinglogic_1_stack[5] ? groupinglogic_1_stack[5] : 1'bz;  // Controlled_Buffer controlled_buffer_69
  Pull_Resistor pull_resistor_38 (.node(RFI));
  assign RFI = groupinglogic_1_stack[4] ? groupinglogic_1_stack[4] : 1'bz;  // Controlled_Buffer controlled_buffer_70
  Pull_Resistor pull_resistor_39 (.node(PLR));
  assign PLR = groupinglogic_1_stack[3] ? groupinglogic_1_stack[3] : 1'bz;  // Controlled_Buffer controlled_buffer_71
  Pull_Resistor pull_resistor_40 (.node(PHR));
  assign PHR = groupinglogic_1_stack[2] ? groupinglogic_1_stack[2] : 1'bz;  // Controlled_Buffer controlled_buffer_72
  Pull_Resistor pull_resistor_41 (.node(PHI));
  assign PHI = groupinglogic_1_stack[1] ? groupinglogic_1_stack[1] : 1'bz;  // Controlled_Buffer controlled_buffer_73
  Pull_Resistor pull_resistor_42 (.node(SRST));
  assign SRST = groupinglogic_1_stack[0] ? groupinglogic_1_stack[0] : 1'bz;  // Controlled_Buffer controlled_buffer_74
  Pull_Resistor pull_resistor_43 (.node(WSL));
  assign WSL = RDSP ? RDSP : 1'bz;  // Controlled_Buffer controlled_buffer_75
  Pull_Resistor pull_resistor_44 (.node(WSA));
  assign WSA = RDSP ? RDSP : 1'bz;  // Controlled_Buffer controlled_buffer_76

  // Notes on the sheet:
  //   contents of rom_1 (hex, n*v repeats v):
  //   bf0000 caca ba0000 3baca ba0000 10*bf0000 820000 bf0000 820005 bf0000 e 400000 830000 870000 600000
  //   820000 bf0000 830004 870000 830000 870000 bd0000 be0000 820000 bf0000 820005 bf0000 e 400000 830000
  //   870000 600000 820000 bf0000 830004 870000 830000 870000 bd0003 be0000 65233*bf0000 800000 bd000e
  //   251*bf0000
  //   jz
  //   jmp
endmodule

module RegCol (
  input  CLK,
  input  [2:0] RSEL,
  input  ACC_WR,
  input  [2:0] WSEL,
  input  [15:0] DIN,
  input  ENBL,
  input  RX,
  input  RH,
  input  RL,
  input  WX,
  input  WH,
  input  WL,
  output [15:0] ACC_OUT,
  output [15:0] DOUT,
  output [15:0] RRA_OUT
);

  wire and_1_out, and_2_out, and_3_out, and_4_out, and_5_out, and_6_out, and_7_out, and_8_out, and_9_out,
       and_10_out, and_11_out, and_12_out, and_13_out, and_14_out, and_15_out, controlled_buffer_1_out,
       decoder_1_out0, decoder_1_out1, decoder_1_out2, decoder_1_out3, decoder_1_out4, decoder_2_out0,
       decoder_2_out1, decoder_2_out2, decoder_2_out3, decoder_2_out4;
  wire [15:0] RA_qh, RA_ql, RA_qx, RB_qh, RB_ql, RB_qx, RC_qh, RC_ql, RC_qx, RD_qh, RD_ql, RD_qx, RRA_qh,
       RRA_ql, RRA_qx;

  Decoder #(.enable("false"), .select(3)) decoder_1 (
    .out0(decoder_1_out0), .out1(decoder_1_out1), .out2(decoder_1_out2), .out3(decoder_1_out3),
    .out4(decoder_1_out4), .sel(RSEL));  // open: out5, out6, out7
  Reg16 RA (
    .D(DIN), .WH(WH), .WL(WL), .CLK(CLK), .WE(decoder_2_out0), .WX(controlled_buffer_1_out),
    .RE(decoder_1_out0), .RL(RL), .RH(RH), .RX(RX), .QH(RA_qh), .QX(RA_qx), .DDO(ACC_OUT), .QL(RA_ql));
  Reg16 RB (
    .D(DIN), .WH(WH), .WL(WL), .CLK(CLK), .WE(decoder_2_out1), .WX(WX), .RE(decoder_1_out1), .RL(RL),
    .RH(RH), .RX(RX), .QH(RB_qh), .QX(RB_qx), .QL(RB_ql));  // open: DDO
  Reg16 RC (
    .D(DIN), .WH(WH), .WL(WL), .CLK(CLK), .WE(decoder_2_out2), .WX(WX), .RE(decoder_1_out2), .RL(RL),
    .RH(RH), .RX(RX), .QH(RC_qh), .QX(RC_qx), .QL(RC_ql));  // open: DDO
  Reg16 RD (
    .D(DIN), .WH(WH), .WL(WL), .CLK(CLK), .WE(decoder_2_out3), .WX(WX), .RE(decoder_1_out3), .RL(RL),
    .RH(RH), .RX(RX), .QH(RD_qh), .QX(RD_qx), .QL(RD_ql));  // open: DDO
  Reg16 RRA (
    .D(DIN), .WH(WH), .WL(WL), .CLK(CLK), .WE(decoder_2_out4), .WX(WX), .RE(decoder_1_out4), .RL(RL),
    .RH(RH), .RX(RX), .QH(RRA_qh), .QX(RRA_qx), .DDO(RRA_OUT), .QL(RRA_ql));
  assign controlled_buffer_1_out = ACC_WR ? ACC_WR : 1'bz;  // Controlled_Buffer controlled_buffer_1
  Pull_Resistor pull_resistor_1 (.node(controlled_buffer_1_out));
  assign controlled_buffer_1_out = WX ? WX : 1'bz;  // Controlled_Buffer controlled_buffer_2
  Decoder #(.enable("false"), .select(3)) decoder_2 (
    .out0(decoder_2_out0), .out1(decoder_2_out1), .out2(decoder_2_out2), .out3(decoder_2_out3),
    .out4(decoder_2_out4), .sel(WSEL));  // open: out5, out6, out7
  and and_1 (and_1_out, decoder_1_out0, RH);
  assign DOUT = and_1_out ? RA_qh : 16'bz;  // Controlled_Buffer controlled_buffer_3
  and and_2 (and_2_out, decoder_1_out0, RX);
  assign DOUT = and_2_out ? RA_qx : 16'bz;  // Controlled_Buffer controlled_buffer_4
  and and_3 (and_3_out, decoder_1_out1, RH);
  assign DOUT = and_3_out ? RB_qh : 16'bz;  // Controlled_Buffer controlled_buffer_5
  and and_4 (and_4_out, decoder_1_out1, RX);
  assign DOUT = and_4_out ? RB_qx : 16'bz;  // Controlled_Buffer controlled_buffer_6
  and and_5 (and_5_out, decoder_1_out2, RH);
  assign DOUT = and_5_out ? RC_qh : 16'bz;  // Controlled_Buffer controlled_buffer_7
  and and_6 (and_6_out, decoder_1_out2, RX);
  assign DOUT = and_6_out ? RC_qx : 16'bz;  // Controlled_Buffer controlled_buffer_8
  and and_7 (and_7_out, decoder_1_out3, RH);
  assign DOUT = and_7_out ? RD_qh : 16'bz;  // Controlled_Buffer controlled_buffer_9
  and and_8 (and_8_out, decoder_1_out3, RX);
  assign DOUT = and_8_out ? RD_qx : 16'bz;  // Controlled_Buffer controlled_buffer_10
  and and_9 (and_9_out, decoder_1_out4, RH);
  assign DOUT = and_9_out ? RRA_qh : 16'bz;  // Controlled_Buffer controlled_buffer_11
  and and_10 (and_10_out, decoder_1_out4, RX);
  assign DOUT = and_10_out ? RRA_qx : 16'bz;  // Controlled_Buffer controlled_buffer_12
  and and_11 (and_11_out, decoder_1_out0, RL);
  assign DOUT = and_11_out ? RA_ql : 16'bz;  // Controlled_Buffer controlled_buffer_13
  and and_12 (and_12_out, decoder_1_out1, RL);
  assign DOUT = and_12_out ? RB_ql : 16'bz;  // Controlled_Buffer controlled_buffer_14
  and and_13 (and_13_out, decoder_1_out2, RL);
  assign DOUT = and_13_out ? RC_ql : 16'bz;  // Controlled_Buffer controlled_buffer_15
  and and_14 (and_14_out, decoder_1_out3, RL);
  assign DOUT = and_14_out ? RD_ql : 16'bz;  // Controlled_Buffer controlled_buffer_16
  and and_15 (and_15_out, decoder_1_out4, RL);
  assign DOUT = and_15_out ? RRA_ql : 16'bz;  // Controlled_Buffer controlled_buffer_17
endmodule

module Reg16 (
  input  RE,
  input  WE,
  input  RH,
  input  WX,
  input  RX,
  input  WH,
  input  RL,
  input  WL,
  input  CLK,
  input  [15:0] D,
  output [15:0] QH,
  output [15:0] QX,
  output [15:0] DDO,
  output [15:0] QL
);

  wire and_1_out, and_2_out, and_3_out, and_4_out, and_5_out, or_1_out, or_2_out;
  wire [7:0] controlled_buffer_2_out, pull_resistor_1_node;

  or or_1 (or_1_out, WX, WH);
  or or_2 (or_2_out, WX, WL);
  Register AH (.D(D[15:8]), .en(and_1_out), .clk(CLK), .Q(DDO[15:8]));  // open: clr
  and and_1 (and_1_out, WE, or_1_out);
  Register AL (.D(D[7:0]), .en(and_2_out), .clk(CLK), .Q(DDO[7:0]));  // open: clr
  and and_2 (and_2_out, WE, or_2_out);
  and and_3 (and_3_out, RX, RE);
  assign QX = and_3_out ? DDO : 16'bz;  // Controlled_Buffer controlled_buffer_1
  and and_4 (and_4_out, RL, RE);
  assign controlled_buffer_2_out = and_4_out ? DDO[7:0] : 8'bz;  // Controlled_Buffer controlled_buffer_2
  and and_5 (and_5_out, RH, RE);
  Pull_Resistor pull_resistor_1 (.node(pull_resistor_1_node));
  assign QH = {{8{1'b0}}, pull_resistor_1_node};  // Bit_Extender bit_extender_1
  assign pull_resistor_1_node = and_5_out ? DDO[15:8] : 8'bz;  // Controlled_Buffer controlled_buffer_3
  Pull_Resistor pull_resistor_2 (.node(QX));
  Pull_Resistor pull_resistor_3 (.node(controlled_buffer_2_out));
  assign QL = {{8{1'b0}}, controlled_buffer_2_out};  // Bit_Extender bit_extender_2
endmodule

module IP (
  input  JMP,
  input  CLK,
  input  [15:0] JMPLOC,
  output [15:0] IPOUT
);

  wire del_not16_1_q, del_not16_2_q, del_not16_3_q, pull_resistor_3_node, rgbled_1_p1, rgbled_1_p2,
       rgbled_1_p3;
  wire [15:0] controlled_buffer_4_out;

  // RGBLED rgbled_1: pin names not known; wires that end beside it: rgbled_1_p1, rgbled_1_p2, rgbled_1_p3
  Pull_Resistor pull_resistor_1 (.node(rgbled_1_p1));
  assign rgbled_1_p1 = JMP ? JMP : 1'bz;  // Controlled_Buffer controlled_buffer_1
  Pull_Resistor pull_resistor_2 (.node(rgbled_1_p3));
  assign rgbled_1_p3 = CLK ? CLK : 1'bz;  // Controlled_Buffer controlled_buffer_2
  assign rgbled_1_p3 = del_not16_1_q ? del_not16_1_q : 1'bz;  // Controlled_Buffer controlled_buffer_3
  DEL_NOT16 del_not16_1 (.D(del_not16_2_q), .Q(del_not16_1_q));
  DEL_NOT16 del_not16_2 (.D(del_not16_3_q), .Q(del_not16_2_q));
  DEL_NOT16 del_not16_3 (.D(rgbled_1_p2), .Q(del_not16_3_q));
  assign controlled_buffer_4_out = rgbled_1_p1 ? JMPLOC : 16'bz;  // Controlled_Buffer controlled_buffer_4
  assign controlled_buffer_4_out = rgbled_1_p2 ? 16'hff00 : 16'bz;  // Controlled_Buffer controlled_buffer_5
  Counter #(.max('hffff), .width(16)) counter_1 (
    .load(pull_resistor_3_node), .clk(rgbled_1_p3), .D(controlled_buffer_4_out), .Q(IPOUT));  // open: clr, up, count, carry
  Pull_Resistor pull_resistor_3 (.node(pull_resistor_3_node));
  assign pull_resistor_3_node = rgbled_1_p1 ? rgbled_1_p1 : 1'bz;  // Controlled_Buffer controlled_buffer_6
  assign pull_resistor_3_node = rgbled_1_p2 ? rgbled_1_p2 : 1'bz;  // Controlled_Buffer controlled_buffer_7
  assign pull_resistor_3_node = rgbled_1_p2 ? rgbled_1_p2 : 1'bz;  // Controlled_Buffer controlled_buffer_8
  POR por_1 (.out(rgbled_1_p2));

  // Notes on the sheet:
  //   Reset Vector
endmodule

module InstructionParser (
  input  [23:0] Instruction,
  output Cat0,
  output [2:0] Category,
  output [4:0] Subinstruction,
  output [7:0] OperandHigh,
  output [7:0] OperandLow,
  output [15:0] OperandFull
);

  nor nor_1 (Cat0, Instruction[23], Instruction[22], Instruction[21]);
  LED NorCat (.in(Cat0));
  LED Si_Bit0 (.in(Instruction[16]));
  LED Si_Bit1 (.in(Instruction[17]));
  LED Si_Bit2 (.in(Instruction[18]));
  LED Si_Bit3 (.in(Instruction[19]));
  LED Si_Bit4 (.in(Instruction[20]));
  // RGBLED CategoryLED: pin names not known; wires that end beside it: Instruction[23], Instruction[22], Instruction[21]

  assign Category = Instruction[23:21];
  assign OperandFull = Instruction[15:0];
  assign OperandHigh = Instruction[15:8];
  assign OperandLow = Instruction[7:0];
  assign Subinstruction = Instruction[20:16];
endmodule

module SplittingLogic (
  input  [23:0] ROM_IN,
  input  Execute,
  output [15:0] OperandX,
  output [7:0] OperandLo,
  output Cat_0,
  output Cat_1,
  output [7:0] OperandHi,
  output Cat_2,
  output Cat_3,
  output Cat_4,
  output Cat_5,
  output Cat_6,
  output Cat_7,
  output i0,
  output i1,
  output i2,
  output i3,
  output i4,
  output i5,
  output i6,
  output i7,
  output i8,
  output i9,
  output i10,
  output i11,
  output i12,
  output i13,
  output i14,
  output i15,
  output i16,
  output i17,
  output i18,
  output i19,
  output i20,
  output i21,
  output i22,
  output i23,
  output i24,
  output i25,
  output i26,
  output i27,
  output i28,
  output i29,
  output i30,
  output i31
);

  wire [2:0] Parser_category;
  wire [4:0] Parser_subinstruction;

  Decoder #(.select(3)) decoder_1 (
    .out0(Cat_0), .out1(Cat_1), .out2(Cat_2), .out3(Cat_3), .out4(Cat_4), .out5(Cat_5), .out6(Cat_6),
    .out7(Cat_7), .sel(Parser_category), .en(Execute));
  Decoder #(.select(5)) decoder_2 (
    .out0(i0), .out1(i1), .out2(i2), .out3(i3), .out4(i4), .out5(i5), .out6(i6), .out7(i7), .out8(i8),
    .out9(i9), .out10(i10), .out11(i11), .out12(i12), .out13(i13), .out14(i14), .out15(i15), .out16(i16),
    .out17(i17), .out18(i18), .out19(i19), .out20(i20), .out21(i21), .out22(i22), .out23(i23), .out24(i24),
    .out25(i25), .out26(i26), .out27(i27), .out28(i28), .out29(i29), .out30(i30), .out31(i31),
    .sel(Parser_subinstruction), .en(Execute));
  // Probe on ROM_IN
  InstructionParser Parser (
    .Instruction(ROM_IN), .Category(Parser_category), .Subinstruction(Parser_subinstruction),
    .OperandHigh(OperandHi), .OperandLow(OperandLo), .OperandFull(OperandX));  // open: Cat0
endmodule

module GroupingLogic (
  input  Execute,
  input  [23:0] Instruction,
  output [7:0] HI,
  output [7:0] LO,
  output [15:0] X,
  output [31:0] ILOAD,
  output [31:0] RLOAD,
  output [31:0] STORE,
  output [31:0] ALU,
  output [31:0] STACK,
  output [31:0] MISC,
  output [31:0] RESERVED1,
  output [31:0] RESERVED2
);

  wire splittinglogic_1_cat_0, splittinglogic_1_cat_1, splittinglogic_1_cat_2, splittinglogic_1_cat_3,
       splittinglogic_1_cat_4, splittinglogic_1_cat_5, splittinglogic_1_cat_6, splittinglogic_1_cat_7;
  wire [31:0] splittinglogic_1_i0;

  SplittingLogic splittinglogic_1 (
    .Execute(Execute), .ROM_IN(Instruction), .Cat_1(splittinglogic_1_cat_1), .Cat_7(splittinglogic_1_cat_7),
    .Cat_2(splittinglogic_1_cat_2), .Cat_6(splittinglogic_1_cat_6), .Cat_3(splittinglogic_1_cat_3),
    .Cat_5(splittinglogic_1_cat_5), .i1(splittinglogic_1_i0[1]), .i3(splittinglogic_1_i0[3]),
    .i5(splittinglogic_1_i0[5]), .i7(splittinglogic_1_i0[7]), .i9(splittinglogic_1_i0[9]),
    .i11(splittinglogic_1_i0[11]), .i13(splittinglogic_1_i0[13]), .i15(splittinglogic_1_i0[15]),
    .i17(splittinglogic_1_i0[17]), .i19(splittinglogic_1_i0[19]), .i21(splittinglogic_1_i0[21]),
    .i23(splittinglogic_1_i0[23]), .i25(splittinglogic_1_i0[25]), .i27(splittinglogic_1_i0[27]),
    .i29(splittinglogic_1_i0[29]), .i31(splittinglogic_1_i0[31]), .Cat_4(splittinglogic_1_cat_4),
    .i0(splittinglogic_1_i0[0]), .i2(splittinglogic_1_i0[2]), .i4(splittinglogic_1_i0[4]),
    .i6(splittinglogic_1_i0[6]), .i8(splittinglogic_1_i0[8]), .i10(splittinglogic_1_i0[10]),
    .i12(splittinglogic_1_i0[12]), .i14(splittinglogic_1_i0[14]), .i16(splittinglogic_1_i0[16]),
    .i18(splittinglogic_1_i0[18]), .i20(splittinglogic_1_i0[20]), .i22(splittinglogic_1_i0[22]),
    .i24(splittinglogic_1_i0[24]), .i26(splittinglogic_1_i0[26]), .i28(splittinglogic_1_i0[28]),
    .i30(splittinglogic_1_i0[30]), .OperandHi(HI), .OperandLo(LO), .OperandX(X),
    .Cat_0(splittinglogic_1_cat_0));
  Pull_Resistor pull_resistor_1 (.node(ILOAD));
  assign ILOAD = splittinglogic_1_cat_0 ? splittinglogic_1_i0 : 32'bz;  // Controlled_Buffer controlled_buffer_1
  Pull_Resistor pull_resistor_2 (.node(RLOAD));
  assign RLOAD = splittinglogic_1_cat_1 ? splittinglogic_1_i0 : 32'bz;  // Controlled_Buffer controlled_buffer_2
  Pull_Resistor pull_resistor_3 (.node(STORE));
  assign STORE = splittinglogic_1_cat_2 ? splittinglogic_1_i0 : 32'bz;  // Controlled_Buffer controlled_buffer_3
  Pull_Resistor pull_resistor_4 (.node(ALU));
  assign ALU = splittinglogic_1_cat_3 ? splittinglogic_1_i0 : 32'bz;  // Controlled_Buffer controlled_buffer_4
  Pull_Resistor pull_resistor_5 (.node(STACK));
  assign STACK = splittinglogic_1_cat_4 ? splittinglogic_1_i0 : 32'bz;  // Controlled_Buffer controlled_buffer_5
  Pull_Resistor pull_resistor_6 (.node(MISC));
  assign MISC = splittinglogic_1_cat_5 ? splittinglogic_1_i0 : 32'bz;  // Controlled_Buffer controlled_buffer_6
  Pull_Resistor pull_resistor_7 (.node(RESERVED1));
  assign RESERVED1 = splittinglogic_1_cat_6 ? splittinglogic_1_i0 : 32'bz;  // Controlled_Buffer controlled_buffer_7
  Pull_Resistor pull_resistor_8 (.node(RESERVED2));
  assign RESERVED2 = splittinglogic_1_cat_7 ? splittinglogic_1_i0 : 32'bz;  // Controlled_Buffer controlled_buffer_8
  LED ILOAD_LED (.in(splittinglogic_1_cat_0));
  LED RLOAD_LED (.in(splittinglogic_1_cat_1));
  LED STORE_LED (.in(splittinglogic_1_cat_2));
  LED ALU_LED (.in(splittinglogic_1_cat_3));
  LED STACK_LED (.in(splittinglogic_1_cat_4));
  LED MISC_LED (.in(splittinglogic_1_cat_5));
endmodule

module test (
  input  [15:0] in_1,
  input  POP,
  input  PUSH,
  input  [15:0] PUSH_VAL,
  input  LDSP,
  input  [7:0] SI,
  input  INIT,
  output [15:0] RAM_ADDR,
  output RAM_WE,
  output [15:0] RAM_VAL,
  output [15:0] POP_VAL,
  output [15:0] SPOUT
);

  wire and_1_out, clock_1_out, comparator_1_gt, comparator_2_lt, controlled_buffer_1_out,
       controlled_buffer_4_out, counter_1_carry, del_not16_1_q, del_not16_2_q, lowclock_1_clksig, nor_1_out,
       not_1_out, pull_resistor_1_node, splittinglogic_1_cat_0, splittinglogic_1_cat_1,
       splittinglogic_1_cat_2, splittinglogic_1_cat_3, splittinglogic_1_cat_4, splittinglogic_1_cat_5,
       splittinglogic_1_cat_6, splittinglogic_1_cat_7, splittinglogic_1_i0, splittinglogic_1_i1,
       splittinglogic_1_i2, splittinglogic_1_i3, splittinglogic_1_i4, splittinglogic_1_i5,
       splittinglogic_1_i6, splittinglogic_1_i7, splittinglogic_1_i8, splittinglogic_1_i9,
       splittinglogic_1_i10, splittinglogic_1_i11, splittinglogic_1_i12, splittinglogic_1_i13,
       splittinglogic_1_i14, splittinglogic_1_i15, splittinglogic_1_i16, splittinglogic_1_i17,
       splittinglogic_1_i18, splittinglogic_1_i19, splittinglogic_1_i20, splittinglogic_1_i21,
       splittinglogic_1_i22, splittinglogic_1_i23, splittinglogic_1_i24, splittinglogic_1_i25,
       splittinglogic_1_i26, splittinglogic_1_i27, splittinglogic_1_i28, splittinglogic_1_i29,
       splittinglogic_1_i30, splittinglogic_1_i31, xor_1_out;
  wire [3:0] bit_extender_1_out;
  wire [7:0] controlled_buffer_2_out, undriven, undriven_2;
  wire [15:0] register_1_q, undriven_3;
  wire [23:16] counter_1_q;

  Counter #(.max('h1f), .width(5)) counter_1 (
    .clk(clock_1_out), .carry(counter_1_carry), .Q(counter_1_q[20:16]));  // open: clr, load, up, count, D
  Clock clock_1 (.out(clock_1_out));
  assign controlled_buffer_1_out = LDSP ? LDSP : 1'bz;  // Controlled_Buffer controlled_buffer_1
  assign controlled_buffer_2_out = LDSP ? SI : 8'bz;  // Controlled_Buffer controlled_buffer_2
  Counter #(.max('h7), .width(3)) counter_2 (
    .clk(counter_1_carry), .Q(counter_1_q[23:21]));  // open: clr, load, up, count, D, carry
  DEL_NOT16 del_not16_1 (.D(POP), .Q(del_not16_1_q));
  DEL_NOT16 del_not16_2 (.D(del_not16_1_q), .Q(del_not16_2_q));
  assign controlled_buffer_1_out = INIT ? INIT : 1'bz;  // Controlled_Buffer controlled_buffer_3
  nor nor_1 (nor_1_out, ~PUSH, del_not16_2_q);  // NOR_Gate
  assign controlled_buffer_4_out = nor_1_out ? nor_1_out : 1'bz;  // Controlled_Buffer controlled_buffer_4
  Pull_Resistor pull_resistor_1 (.node(pull_resistor_1_node));
  xor xor_1 (xor_1_out, del_not16_2_q, PUSH);
  assign pull_resistor_1_node = xor_1_out ? xor_1_out : 1'bz;  // Controlled_Buffer controlled_buffer_5
  Pull_Resistor pull_resistor_2 ();  // open: node
  Pull_Resistor pull_resistor_3 (.node(controlled_buffer_1_out));
  assign controlled_buffer_2_out = INIT ? {8{1'b0}} : 8'bz;  // Controlled_Buffer controlled_buffer_6
  SplittingLogic splittinglogic_1 (
    .ROM_IN({counter_1_q, undriven_2, undriven}), .Cat_1(splittinglogic_1_cat_1),
    .Cat_7(splittinglogic_1_cat_7), .Cat_2(splittinglogic_1_cat_2), .Cat_6(splittinglogic_1_cat_6),
    .Cat_3(splittinglogic_1_cat_3), .Cat_5(splittinglogic_1_cat_5), .i1(splittinglogic_1_i1),
    .i3(splittinglogic_1_i3), .i5(splittinglogic_1_i5), .i7(splittinglogic_1_i7), .i9(splittinglogic_1_i9),
    .i11(splittinglogic_1_i11), .i13(splittinglogic_1_i13), .i15(splittinglogic_1_i15),
    .i17(splittinglogic_1_i17), .i19(splittinglogic_1_i19), .i21(splittinglogic_1_i21),
    .i23(splittinglogic_1_i23), .i25(splittinglogic_1_i25), .i27(splittinglogic_1_i27),
    .i29(splittinglogic_1_i29), .i31(splittinglogic_1_i31), .Cat_4(splittinglogic_1_cat_4),
    .i0(splittinglogic_1_i0), .i2(splittinglogic_1_i2), .i4(splittinglogic_1_i4), .i6(splittinglogic_1_i6),
    .i8(splittinglogic_1_i8), .i10(splittinglogic_1_i10), .i12(splittinglogic_1_i12),
    .i14(splittinglogic_1_i14), .i16(splittinglogic_1_i16), .i18(splittinglogic_1_i18),
    .i20(splittinglogic_1_i20), .i22(splittinglogic_1_i22), .i24(splittinglogic_1_i24),
    .i26(splittinglogic_1_i26), .i28(splittinglogic_1_i28), .i30(splittinglogic_1_i30),
    .Cat_0(splittinglogic_1_cat_0));  // open: Execute, OperandHi, OperandLo, OperandX
  Counter #(.max('hfefe), .width(16)) counter_3 (
    .load(controlled_buffer_1_out), .up(controlled_buffer_4_out), .clk(pull_resistor_1_node),
    .D({8'hfe, controlled_buffer_2_out}), .Q(RAM_ADDR));  // open: clr, count, carry
  Pull_Resistor pull_resistor_4 (.node(controlled_buffer_4_out));
  assign controlled_buffer_4_out = controlled_buffer_1_out ? controlled_buffer_1_out : 1'bz;  // Controlled_Buffer controlled_buffer_7
  assign pull_resistor_1_node = controlled_buffer_1_out ? controlled_buffer_1_out : 1'bz;  // Controlled_Buffer controlled_buffer_8
  LedBar ledbar_1 (
    .led0(splittinglogic_1_cat_0), .led1(splittinglogic_1_cat_1), .led2(splittinglogic_1_cat_2),
    .led3(splittinglogic_1_cat_3), .led4(splittinglogic_1_cat_4), .led5(splittinglogic_1_cat_5),
    .led6(splittinglogic_1_cat_6), .led7(splittinglogic_1_cat_7));
  LedBar ledbar_2 (
    .led0(splittinglogic_1_i31), .led1(splittinglogic_1_i30), .led2(splittinglogic_1_i29),
    .led3(splittinglogic_1_i28), .led4(splittinglogic_1_i27), .led5(splittinglogic_1_i26),
    .led6(splittinglogic_1_i25), .led7(splittinglogic_1_i24));
  LedBar ledbar_3 (
    .led0(splittinglogic_1_i23), .led1(splittinglogic_1_i22), .led2(splittinglogic_1_i21),
    .led3(splittinglogic_1_i20), .led4(splittinglogic_1_i19), .led5(splittinglogic_1_i18),
    .led6(splittinglogic_1_i17), .led7(splittinglogic_1_i16));
  LedBar ledbar_4 (
    .led0(splittinglogic_1_i15), .led1(splittinglogic_1_i14), .led2(splittinglogic_1_i13),
    .led3(splittinglogic_1_i12), .led4(splittinglogic_1_i11), .led5(splittinglogic_1_i10),
    .led6(splittinglogic_1_i9), .led7(splittinglogic_1_i8));
  LedBar ledbar_5 (
    .led0(splittinglogic_1_i7), .led1(splittinglogic_1_i6), .led2(splittinglogic_1_i5),
    .led3(splittinglogic_1_i4), .led4(splittinglogic_1_i3), .led5(splittinglogic_1_i2),
    .led6(splittinglogic_1_i1), .led7(splittinglogic_1_i0));
  Comparator #(.mode("unsigned"), .width(16)) comparator_1 (
    .a(in_1), .b(16'hfddf), .gt(comparator_1_gt));  // open: eq, lt
  Comparator #(.mode("unsigned"), .width(16)) comparator_2 (
    .a(in_1), .b(16'hfde5), .lt(comparator_2_lt));  // open: gt, eq
  LowClock lowclock_1 (.CLKSIG(lowclock_1_clksig));
  Bit_Extender #(.in_width(16), .out_width(4), .\type ("zero")) bit_extender_1 (.in(in_1), .out(bit_extender_1_out));
  and and_1 (and_1_out, comparator_1_gt, comparator_2_lt);
  not not_1 (not_1_out, and_1_out);
  Decoder #(.select(4)) decoder_1 (
    .sel(bit_extender_1_out), .en(and_1_out));  // open: out0, out1, out2, out3, out4, out5, out6, out7, out8, out9, out10, out11, out12, out13, out14, out15
  Register #(.width(16)) register_1 (.D(undriven_3), .Q(register_1_q));  // open: en, clk, clr
  Register #(.width(16)) register_2 (.D(undriven_3), .Q(register_1_q));  // open: en, clk, clr
  Register #(.width(16)) register_3 (.D(undriven_3), .Q(register_1_q));  // open: en, clk, clr
  RAM #(.addrWidth(16), .dataWidth(16), .enables("line")) ram_1 (
    .addr(in_1), .we(not_1_out), .clk(lowclock_1_clksig));  // open: din, dout
  Register #(.width(16)) register_4 (.D(undriven_3), .Q(register_1_q));  // open: en, clk, clr
  Register #(.width(16)) register_5 (.D(undriven_3), .Q(register_1_q));  // open: en, clk, clr
  Register #(.width(16)) register_6 (.D(undriven_3), .Q(register_1_q));  // open: en, clk, clr
  Register #(.width(16)) register_7 (.D(undriven_3), .Q(register_1_q));  // open: en, clk, clr
  Register #(.width(16)) register_8 (.D(undriven_3), .Q(register_1_q));  // open: en, clk, clr
  Register #(.width(16)) register_9 (.D(undriven_3), .Q(register_1_q));  // open: en, clk, clr
  Register #(.width(16)) register_10 (.D(undriven_3), .Q(register_1_q));  // open: en, clk, clr
  Register #(.width(16)) register_11 (.D(undriven_3), .Q(register_1_q));  // open: en, clk, clr
  Register #(.width(16)) register_12 (.D(undriven_3), .Q(register_1_q));  // open: en, clk, clr

  assign RAM_VAL = PUSH_VAL;
  assign RAM_WE = PUSH;
  assign SPOUT = RAM_ADDR;

  // Notes on the sheet:
  //   TOP
endmodule

module Stack256 (
  input  POP,
  input  PUSH,
  input  [15:0] PUSH_VAL,
  input  LDSP,
  input  [7:0] SPIN,
  input  INIT,
  output [15:0] RAM_ADDR,
  output RAM_WE,
  output [15:0] RAM_VAL,
  output [15:0] POP_VAL,
  output [15:0] SPOUT
);

  wire controlled_buffer_1_out, controlled_buffer_4_out, del_not16_1_q, del_not16_2_q, nor_1_out,
       pull_resistor_1_node, xor_1_out;
  wire [7:0] controlled_buffer_2_out;

  assign controlled_buffer_1_out = LDSP ? LDSP : 1'bz;  // Controlled_Buffer controlled_buffer_1
  assign controlled_buffer_2_out = LDSP ? SPIN : 8'bz;  // Controlled_Buffer controlled_buffer_2
  DEL_NOT16 del_not16_1 (.D(POP), .Q(del_not16_1_q));
  DEL_NOT16 del_not16_2 (.D(del_not16_1_q), .Q(del_not16_2_q));
  assign controlled_buffer_1_out = INIT ? INIT : 1'bz;  // Controlled_Buffer controlled_buffer_3
  nor nor_1 (nor_1_out, ~PUSH, del_not16_2_q);  // NOR_Gate
  assign controlled_buffer_4_out = nor_1_out ? nor_1_out : 1'bz;  // Controlled_Buffer controlled_buffer_4
  Pull_Resistor pull_resistor_1 (.node(pull_resistor_1_node));
  xor xor_1 (xor_1_out, del_not16_2_q, PUSH);
  assign pull_resistor_1_node = xor_1_out ? xor_1_out : 1'bz;  // Controlled_Buffer controlled_buffer_5
  Pull_Resistor pull_resistor_2 ();  // open: node
  Pull_Resistor pull_resistor_3 (.node(controlled_buffer_1_out));
  assign controlled_buffer_2_out = INIT ? {8{1'b0}} : 8'bz;  // Controlled_Buffer controlled_buffer_6
  Counter #(.max('hfefe), .width(16)) counter_1 (
    .load(controlled_buffer_1_out), .up(controlled_buffer_4_out), .clk(pull_resistor_1_node),
    .D({8'hfe, controlled_buffer_2_out}), .Q(RAM_ADDR));  // open: clr, count, carry
  Pull_Resistor pull_resistor_4 (.node(controlled_buffer_4_out));
  assign controlled_buffer_4_out = controlled_buffer_1_out ? controlled_buffer_1_out : 1'bz;  // Controlled_Buffer controlled_buffer_7
  assign pull_resistor_1_node = controlled_buffer_1_out ? controlled_buffer_1_out : 1'bz;  // Controlled_Buffer controlled_buffer_8

  assign RAM_VAL = PUSH_VAL;
  assign RAM_WE = PUSH;
  assign SPOUT = RAM_ADDR;

  // Notes on the sheet:
  //   TOP
endmodule

module LowClock (
  output CLKSIG
);

  wire clock_1_out, not_1_out;

  Clock clock_1 (.out(clock_1_out));
  not not_1 (not_1_out, clock_1_out);
  and and_1 (CLKSIG, clock_1_out, not_1_out);
endmodule

module RegColCtrl (
  input  RSRA,
  input  RSD,
  input  RSA,
  input  RSC,
  input  RSB,
  input  WSB,
  input  WSA,
  input  WSC,
  input  WSRA,
  input  WSD,
  output REG_ENBL,
  output [2:0] RSEL,
  output [2:0] WSEL
);

  wire xor_2_out, xor_3_out;

  assign RSEL = RSA ? 3'b000 : 3'bz;  // Controlled_Buffer controlled_buffer_1
  assign RSEL = RSB ? 3'b001 : 3'bz;  // Controlled_Buffer controlled_buffer_2
  xor xor_1 (REG_ENBL, xor_2_out, xor_3_out);
  ExactlyOne xor_2 (.out(xor_2_out), .in0(RSRA), .in1(RSD), .in2(RSC), .in3(RSB), .in4(RSA));
  ExactlyOne xor_3 (.out(xor_3_out), .in0(WSRA), .in1(WSD), .in2(WSC), .in3(WSB), .in4(WSA));
  assign RSEL = RSC ? 3'b010 : 3'bz;  // Controlled_Buffer controlled_buffer_3
  assign WSEL = WSC ? 3'b010 : 3'bz;  // Controlled_Buffer controlled_buffer_4
  assign RSEL = RSD ? 3'b011 : 3'bz;  // Controlled_Buffer controlled_buffer_5
  assign WSEL = WSD ? 3'b011 : 3'bz;  // Controlled_Buffer controlled_buffer_6
  assign RSEL = RSRA ? 3'b100 : 3'bz;  // Controlled_Buffer controlled_buffer_7
  assign WSEL = WSRA ? 3'b100 : 3'bz;  // Controlled_Buffer controlled_buffer_8
  Pull_Resistor pull_resistor_1 (.node(WSEL));
  Pull_Resistor pull_resistor_2 (.node(RSEL));
  assign WSEL = WSA ? 3'b000 : 3'bz;  // Controlled_Buffer controlled_buffer_9
  assign WSEL = WSB ? 3'b001 : 3'bz;  // Controlled_Buffer controlled_buffer_10
endmodule

module MAR (
  input  WE,
  input  [15:0] CS,
  input  CLK,
  input  [15:0] DI,
  output [15:0] DO
);

  wire A, B, C, D, E, F, G, H, I, J, K, L, M, N, O, P;
  wire [3:0] bit_extender_1_out;
  wire [15:0] register_1_q, register_2_q, register_3_q, register_4_q, register_5_q, register_6_q,
       register_7_q, register_8_q, register_9_q, register_10_q, register_11_q, register_12_q, register_13_q,
       register_14_q, register_15_q, register_16_q;

  Bit_Extender #(.in_width(16), .out_width(4), .\type ("zero")) bit_extender_1 (.in(CS), .out(bit_extender_1_out));
  Decoder #(.enable("false"), .select(4)) decoder_1 (
    .out0(A), .out1(B), .out2(C), .out3(D), .out4(E), .out5(F), .out6(G), .out7(H), .out8(P), .out9(O),
    .out10(N), .out11(M), .out12(L), .out13(K), .out14(J), .out15(I), .sel(bit_extender_1_out));
  Register #(.width(16)) register_1 (.D(DI), .en(A), .clk(CLK), .Q(register_1_q));  // open: clr
  Register #(.width(16)) register_2 (.D(DI), .en(B), .clk(CLK), .Q(register_2_q));  // open: clr
  Register #(.width(16)) register_3 (.D(DI), .en(C), .clk(CLK), .Q(register_3_q));  // open: clr
  Register #(.width(16)) register_4 (.D(DI), .en(D), .clk(CLK), .Q(register_4_q));  // open: clr
  Register #(.width(16)) register_5 (.D(DI), .en(E), .clk(CLK), .Q(register_5_q));  // open: clr
  assign DO = A ? register_1_q : 16'bz;  // Controlled_Buffer controlled_buffer_1
  Register #(.width(16)) register_6 (.D(DI), .en(F), .clk(CLK), .Q(register_6_q));  // open: clr
  assign DO = B ? register_2_q : 16'bz;  // Controlled_Buffer controlled_buffer_2
  Register #(.width(16)) register_7 (.D(DI), .en(G), .clk(CLK), .Q(register_7_q));  // open: clr
  assign DO = C ? register_3_q : 16'bz;  // Controlled_Buffer controlled_buffer_3
  Register #(.width(16)) register_8 (.D(DI), .en(H), .clk(CLK), .Q(register_8_q));  // open: clr
  assign DO = D ? register_4_q : 16'bz;  // Controlled_Buffer controlled_buffer_4
  Register #(.width(16)) register_9 (.D(DI), .en(I), .clk(CLK), .Q(register_9_q));  // open: clr
  assign DO = E ? register_5_q : 16'bz;  // Controlled_Buffer controlled_buffer_5
  Register #(.width(16)) register_10 (.D(DI), .en(J), .clk(CLK), .Q(register_10_q));  // open: clr
  assign DO = F ? register_6_q : 16'bz;  // Controlled_Buffer controlled_buffer_6
  Register #(.width(16)) register_11 (.D(DI), .en(K), .clk(CLK), .Q(register_11_q));  // open: clr
  assign DO = G ? register_7_q : 16'bz;  // Controlled_Buffer controlled_buffer_7
  Register #(.width(16)) register_12 (.D(DI), .en(L), .clk(CLK), .Q(register_12_q));  // open: clr
  assign DO = H ? register_8_q : 16'bz;  // Controlled_Buffer controlled_buffer_8
  assign DO = I ? register_9_q : 16'bz;  // Controlled_Buffer controlled_buffer_9
  assign DO = J ? register_10_q : 16'bz;  // Controlled_Buffer controlled_buffer_10
  assign DO = K ? register_11_q : 16'bz;  // Controlled_Buffer controlled_buffer_11
  assign DO = L ? register_12_q : 16'bz;  // Controlled_Buffer controlled_buffer_12
  Register #(.width(16)) register_13 (.D(DI), .en(L), .clk(CLK), .Q(register_13_q));  // open: clr
  Register #(.width(16)) register_14 (.D(DI), .en(M), .clk(CLK), .Q(register_14_q));  // open: clr
  Register #(.width(16)) register_15 (.D(DI), .en(N), .clk(CLK), .Q(register_15_q));  // open: clr
  Register #(.width(16)) register_16 (.D(DI), .en(O), .clk(CLK), .Q(register_16_q));  // open: clr
  assign DO = L ? register_13_q : 16'bz;  // Controlled_Buffer controlled_buffer_13
  assign DO = M ? register_14_q : 16'bz;  // Controlled_Buffer controlled_buffer_14
  assign DO = N ? register_15_q : 16'bz;  // Controlled_Buffer controlled_buffer_15
  assign DO = O ? register_16_q : 16'bz;  // Controlled_Buffer controlled_buffer_16
endmodule

module ALU16Ctrl (
  input  ALU_INC,
  input  ALU_DEC,
  input  ADD_OP,
  input  SUB_OP,
  input  AND_OP,
  input  OR_OP,
  input  NOT_OP,
  input  NOR_OP,
  input  NAND_OP,
  input  XOR_OP,
  output Q_ENBL,
  output Q_Ci,
  output Q_AINV,
  output Q_BINV,
  output Q_SUM,
  output Q_AND,
  output Q_XOR,
  output Q_OR
);

  ExactlyOne ALU_ENABLE (
    .out(Q_ENBL), .in0(XOR_OP), .in1(NAND_OP), .in2(NOR_OP), .in3(NOT_OP), .in4(OR_OP), .in5(AND_OP),
    .in6(SUB_OP), .in7(ADD_OP), .in8(ALU_DEC), .in9(ALU_INC));
  xor CI_X (Q_Ci, SUB_OP, ALU_DEC);
  ExactlyOne AINV_X (.out(Q_AINV), .in0(NOT_OP), .in1(NOR_OP), .in2(NAND_OP));
  ExactlyOne BINV_X (.out(Q_BINV), .in0(SUB_OP), .in1(NOT_OP), .in2(ALU_DEC), .in3(NOR_OP), .in4(NAND_OP));
  ExactlyOne SUM_X (.out(Q_SUM), .in0(ALU_INC), .in1(ADD_OP), .in2(SUB_OP), .in3(ALU_DEC));
  xor AND_X (Q_AND, AND_OP, NOR_OP);
  buf XOR_X (Q_XOR, XOR_OP);  // XOR_Gate
  ExactlyOne OR_X (.out(Q_OR), .in0(OR_OP), .in1(NOT_OP), .in2(NAND_OP));
endmodule

module BufferedConstruct (
  input  D,
  output Q
);

  Pull_Resistor pull_resistor_1 (.node(Q));
  assign Q = D ? D : 1'bz;  // Controlled_Buffer controlled_buffer_1
endmodule
