// Logisim project matrixdriver.circ as structural Verilog: 2 circuits, main circuit xterm_fbdriver
module xterm_fbdriver (
  input  CLK,
  input  [15:0] drv_ctl,
  output disp_clk,
  output [6:0] X,
  output disp_write,
  output [6:0] Y,
  output [7:0] D,
  output disp_reset
);

  wire decoder_1_out1, decoder_1_out2, del_1_q, del_2_q, not_1_out, or_1_out, XUPDATE_carry;
  wire [7:0] controlled_buffer_3_out;
  wire [13:0] controlled_buffer_1_out, FB_Counter_q, register_1_q, undriven;

  Counter #(.max('h7f), .width(7)) XUPDATE (.clk(CLK), .carry(XUPDATE_carry), .Q(X));  // open: clr, load, up, count, D
  Decoder #(.disabled("Z"), .enable("false"), .select(2)) decoder_1 (
    .out1(decoder_1_out1), .out2(decoder_1_out2), .out3(disp_reset), .sel(drv_ctl[15:14]));  // open: out0
  Counter #(.max('h7f), .width(7)) YUPDATE (.clk(XUPDATE_carry), .Q(Y));  // open: clr, load, up, count, D, carry
  Counter #(.max('h3fff), .width(14)) FB_Counter (
    .clk(CLK), .D(undriven), .Q(FB_Counter_q));  // open: clr, load, up, count, carry
  or or_1 (or_1_out, disp_reset, decoder_1_out2, decoder_1_out1);
  not not_1 (not_1_out, or_1_out);
  assign controlled_buffer_1_out = not_1_out ? FB_Counter_q : 14'bz;  // Controlled_Buffer controlled_buffer_1
  Register #(.width(14)) register_1 (
    .D(drv_ctl[13:0]), .en(decoder_1_out1), .clk(decoder_1_out1), .Q(register_1_q));  // open: clr
  del del_1 (.D(decoder_1_out2), .Q(del_1_q));
  del del_2 (.D(del_1_q), .Q(del_2_q));
  assign controlled_buffer_1_out = or_1_out ? register_1_q : 14'bz;  // Controlled_Buffer controlled_buffer_2
  RAM #(.addrWidth(14), .enables("line")) Hardware_Framebuffer (
    .addr(controlled_buffer_1_out), .we(del_2_q), .clk(CLK), .din(controlled_buffer_3_out), .dout(D));
  assign controlled_buffer_3_out = decoder_1_out2 ? drv_ctl[7:0] : 8'bz;  // Controlled_Buffer controlled_buffer_3

  assign disp_clk = CLK;
  assign disp_write = CLK;

  // Notes on the sheet:
  //   3: display reset
  //   1: framebuffer accepts address input
  //   2: frambuffer inserts given pixel data in ram
  //   0: framebuffer keeps looping
  //   ctl
  //   addr
  //   pixel
endmodule

module del (
  input  D,
  output Q
);

  wire not_1_out, not_2_out, not_3_out, not_4_out, not_5_out, not_6_out, not_8_out, not_9_out, not_10_out,
       not_11_out, not_12_out, not_13_out, not_14_out, not_15_out, not_16_out, not_17_out, not_18_out,
       not_19_out, not_20_out, not_21_out, not_22_out, not_23_out, not_24_out;

  not not_1 (not_1_out, not_4_out);
  not not_2 (not_2_out, not_5_out);
  not not_3 (not_3_out, not_6_out);
  not not_4 (not_4_out, not_2_out);
  not not_5 (not_5_out, not_3_out);
  not not_6 (not_6_out, not_13_out);
  not not_7 (Q, not_10_out);
  not not_8 (not_8_out, not_11_out);
  not not_9 (not_9_out, not_12_out);
  not not_10 (not_10_out, not_8_out);
  not not_11 (not_11_out, not_9_out);
  not not_12 (not_12_out, not_19_out);
  not not_13 (not_13_out, not_16_out);
  not not_14 (not_14_out, not_17_out);
  not not_15 (not_15_out, not_18_out);
  not not_16 (not_16_out, not_14_out);
  not not_17 (not_17_out, not_15_out);
  not not_18 (not_18_out, D);
  not not_19 (not_19_out, not_22_out);
  not not_20 (not_20_out, not_23_out);
  not not_21 (not_21_out, not_24_out);
  not not_22 (not_22_out, not_20_out);
  not not_23 (not_23_out, not_21_out);
  not not_24 (not_24_out, not_1_out);
endmodule
